// Logisim project CSE332.2Lab.circ as structural Verilog: 22 circuits, main circuit main
module main (
);

  AND_7408_2in_IC and_7408_2in_ic_1 ();  // open: out_11, out_12, out_10, out_9, in_5, in_6, in_7, in_8, in_1, in_2, in_3, in_4
  x_dual_4x1_mux x_dual_4x1_mux_1 ();  // open: out_12, out_11, in_7, in_1, in_2, in_3, in_4, in_5, in_6, in_8, in_9, in_10
  OR_7432_2in_IC or_7432_2in_ic_1 ();  // open: out_11, out_12, out_10, out_9, in_5, in_6, in_7, in_8, in_1, in_2, in_3, in_4
  XOR_7486_2in_IC xor_7486_2in_ic_1 ();  // open: out_11, out_12, out_10, out_9, in_5, in_6, in_7, in_8, in_1, in_2, in_3, in_4
  MUX_2x1 mux_2x1_1 ();  // open: out_4, in_1, in_3, in_2
  Inverter_7404_2in_IC inverter_7404_2in_ic_1 ();  // open: out_9, out_10, out_11, out_12, out_7, out_8, in_5, in_6, in_1, in_2, in_3, in_4
  MUX_4x1_IC mux_4x1_ic_1 ();  // open: out_7, in_1, in_2, in_3, in_4, in_5, in_6
endmodule

module AND_7408_2in_IC (
  input  in_1,
  input  in_2,
  input  in_3,
  input  in_4,
  input  in_5,
  input  in_6,
  input  in_7,
  input  in_8,
  output out_9,
  output out_10,
  output out_11,
  output out_12
);

  and and_1 (out_9, in_1, in_2);
  and and_2 (out_10, in_3, in_4);
  and and_3 (out_11, in_5, in_6);
  and and_4 (out_12, in_7, in_8);
endmodule

module OR_7432_2in_IC (
  input  in_1,
  input  in_2,
  input  in_3,
  input  in_4,
  input  in_5,
  input  in_6,
  input  in_7,
  input  in_8,
  output out_9,
  output out_10,
  output out_11,
  output out_12
);

  or or_1 (out_9, in_1, in_2);
  or or_2 (out_10, in_3, in_4);
  or or_3 (out_11, in_5, in_6);
  or or_4 (out_12, in_7, in_8);
endmodule

module XOR_7486_2in_IC (
  input  in_1,
  input  in_2,
  input  in_3,
  input  in_4,
  input  in_5,
  input  in_6,
  input  in_7,
  input  in_8,
  output out_9,
  output out_10,
  output out_11,
  output out_12
);

  xor xor_1 (out_9, in_1, in_2);
  xor xor_2 (out_10, in_3, in_4);
  xor xor_3 (out_11, in_5, in_6);
  xor xor_4 (out_12, in_7, in_8);
endmodule

module Inverter_7404_2in_IC (
  input  in_1,
  input  in_2,
  input  in_3,
  input  in_4,
  input  in_5,
  input  in_6,
  output out_7,
  output out_8,
  output out_9,
  output out_10,
  output out_11,
  output out_12
);

  not not_1 (out_7, in_1);
  not not_2 (out_8, in_2);
  not not_3 (out_9, in_3);
  not not_4 (out_10, in_4);
  not not_5 (out_11, in_5);
  not not_6 (out_12, in_6);
endmodule

module MUX_4x1_IC (
  input  in_1,
  input  in_2,
  input  in_3,
  input  in_4,
  input  in_5,
  input  in_6,
  output out_7
);

  wire and_1_out, and_2_out, and_3_out, and_4_out, not_1_out, not_2_out;

  not not_1 (not_1_out, in_1);
  not not_2 (not_2_out, in_2);
  and and_1 (and_1_out, in_3, not_2_out, not_1_out);
  and and_2 (and_2_out, in_4, not_2_out, in_1);
  and and_3 (and_3_out, in_5, in_2, not_1_out);
  and and_4 (and_4_out, in_6, in_1, in_2);
  or or_1 (out_7, and_1_out, and_2_out, and_3_out, and_4_out);
endmodule

module x_dual_4x1_mux (
  input  in_1,
  input  in_2,
  input  in_3,
  input  in_4,
  input  in_5,
  input  in_6,
  input  in_7,
  input  in_8,
  input  in_9,
  input  in_10,
  output out_11,
  output out_12
);

  MUX_4x1_IC mux_4x1_ic_1 (
    .out_7(out_11), .in_1(in_9), .in_2(in_10), .in_3(in_1), .in_4(in_2), .in_5(in_3), .in_6(in_4));
  MUX_4x1_IC mux_4x1_ic_2 (
    .out_7(out_12), .in_1(in_9), .in_2(in_10), .in_3(in_5), .in_4(in_6), .in_5(in_7), .in_6(in_8));
endmodule

module MUX_2x1 (
  input  in_1,
  input  in_2,
  input  in_3,
  output out_4
);

  wire and_1_out, and_2_out, not_1_out;

  not not_1 (not_1_out, in_3);
  and and_1 (and_1_out, in_1, not_1_out);
  and and_2 (and_2_out, in_2, in_3);
  or or_1 (out_4, and_1_out, and_2_out);
endmodule

module lab_1 (
  input  A1,
  input  B1,
  input  A2,
  input  B2,
  input  S0,
  input  S1,
  output F1,
  output F2
);

  wire and_7408_2in_ic_1_out_9, and_7408_2in_ic_1_out_10, inverter_7404_2in_ic_1_out_7,
       inverter_7404_2in_ic_1_out_8, or_7432_2in_ic_1_out_9, or_7432_2in_ic_1_out_10,
       xor_7486_2in_ic_1_out_9, xor_7486_2in_ic_1_out_10;

  AND_7408_2in_IC and_7408_2in_ic_1 (
    .out_10(and_7408_2in_ic_1_out_10), .out_9(and_7408_2in_ic_1_out_9), .in_1(A1), .in_2(B1), .in_3(A2),
    .in_4(B2));  // open: out_11, out_12, in_5, in_6, in_7, in_8
  OR_7432_2in_IC or_7432_2in_ic_1 (
    .out_10(or_7432_2in_ic_1_out_10), .out_9(or_7432_2in_ic_1_out_9), .in_1(A1), .in_2(B1), .in_3(A2),
    .in_4(B2));  // open: out_11, out_12, in_5, in_6, in_7, in_8
  XOR_7486_2in_IC xor_7486_2in_ic_1 (
    .out_10(xor_7486_2in_ic_1_out_10), .out_9(xor_7486_2in_ic_1_out_9), .in_1(A1), .in_2(B1), .in_3(A2),
    .in_4(B2));  // open: out_11, out_12, in_5, in_6, in_7, in_8
  Inverter_7404_2in_IC inverter_7404_2in_ic_1 (
    .out_7(inverter_7404_2in_ic_1_out_7), .out_8(inverter_7404_2in_ic_1_out_8), .in_1(A1), .in_2(A2));  // open: out_9, out_10, out_11, out_12, in_5, in_6, in_3, in_4
  x_dual_4x1_mux x_dual_4x1_mux_1 (
    .out_12(F2), .out_11(F1), .in_7(xor_7486_2in_ic_1_out_10), .in_1(and_7408_2in_ic_1_out_9),
    .in_2(or_7432_2in_ic_1_out_9), .in_3(xor_7486_2in_ic_1_out_9), .in_4(inverter_7404_2in_ic_1_out_7),
    .in_5(and_7408_2in_ic_1_out_10), .in_6(or_7432_2in_ic_1_out_10), .in_8(inverter_7404_2in_ic_1_out_8),
    .in_9(S1), .in_10(S0));

  // Notes on the sheet:
  //   Abid ahsan Shanto
  //   1921738042
endmodule

module four_bit_adder (
  input  A,
  input  B,
  input  C,
  input  A_2,
  input  B_2,
  input  A_3,
  input  B_3,
  input  A_4,
  input  B_4,
  output D0,
  output D1,
  output D2,
  output D3,
  output Cout
);

  wire and_7408_2in_ic_1_out_9, and_7408_2in_ic_1_out_10, and_7408_2in_ic_2_out_9, and_7408_2in_ic_2_out_10,
       and_7408_2in_ic_3_out_9, and_7408_2in_ic_3_out_10, and_7408_2in_ic_4_out_9, and_7408_2in_ic_4_out_10,
       c1, c2, c3, xor_7486_2in_ic_1_out_9, xor_7486_2in_ic_2_out_9, xor_7486_2in_ic_3_out_9,
       xor_7486_2in_ic_4_out_9;

  XOR_7486_2in_IC xor_7486_2in_ic_1 (
    .out_10(D0), .out_9(xor_7486_2in_ic_1_out_9), .in_1(A), .in_2(B), .in_3(C), .in_4(xor_7486_2in_ic_1_out_9));  // open: out_11, out_12, in_5, in_6, in_7, in_8
  XOR_7486_2in_IC xor_7486_2in_ic_2 (
    .out_10(D1), .out_9(xor_7486_2in_ic_2_out_9), .in_1(A_2), .in_2(B_2), .in_3(c1),
    .in_4(xor_7486_2in_ic_2_out_9));  // open: out_11, out_12, in_5, in_6, in_7, in_8
  XOR_7486_2in_IC xor_7486_2in_ic_3 (
    .out_10(D2), .out_9(xor_7486_2in_ic_3_out_9), .in_1(A_3), .in_2(B_3), .in_3(c2),
    .in_4(xor_7486_2in_ic_3_out_9));  // open: out_11, out_12, in_5, in_6, in_7, in_8
  XOR_7486_2in_IC xor_7486_2in_ic_4 (
    .out_10(D3), .out_9(xor_7486_2in_ic_4_out_9), .in_1(A_4), .in_2(B_4), .in_3(c3),
    .in_4(xor_7486_2in_ic_4_out_9));  // open: out_11, out_12, in_5, in_6, in_7, in_8
  AND_7408_2in_IC and_7408_2in_ic_1 (
    .out_10(and_7408_2in_ic_1_out_10), .out_9(and_7408_2in_ic_1_out_9), .in_1(B), .in_2(A), .in_3(C),
    .in_4(xor_7486_2in_ic_1_out_9));  // open: out_11, out_12, in_5, in_6, in_7, in_8
  AND_7408_2in_IC and_7408_2in_ic_2 (
    .out_10(and_7408_2in_ic_2_out_10), .out_9(and_7408_2in_ic_2_out_9), .in_1(B_2), .in_2(A_2), .in_3(c1),
    .in_4(xor_7486_2in_ic_2_out_9));  // open: out_11, out_12, in_5, in_6, in_7, in_8
  AND_7408_2in_IC and_7408_2in_ic_3 (
    .out_10(and_7408_2in_ic_3_out_10), .out_9(and_7408_2in_ic_3_out_9), .in_1(B_3), .in_2(A_3), .in_3(c2),
    .in_4(xor_7486_2in_ic_3_out_9));  // open: out_11, out_12, in_5, in_6, in_7, in_8
  AND_7408_2in_IC and_7408_2in_ic_4 (
    .out_10(and_7408_2in_ic_4_out_10), .out_9(and_7408_2in_ic_4_out_9), .in_1(B_4), .in_2(A_4), .in_3(c3),
    .in_4(xor_7486_2in_ic_4_out_9));  // open: out_11, out_12, in_5, in_6, in_7, in_8
  OR_7432_2in_IC or_7432_2in_ic_1 (
    .out_9(c1), .in_1(and_7408_2in_ic_1_out_9), .in_2(and_7408_2in_ic_1_out_10));  // open: out_11, out_12, out_10, in_5, in_6, in_7, in_8, in_3, in_4
  OR_7432_2in_IC or_7432_2in_ic_2 (
    .out_9(c2), .in_1(and_7408_2in_ic_2_out_9), .in_2(and_7408_2in_ic_2_out_10));  // open: out_11, out_12, out_10, in_5, in_6, in_7, in_8, in_3, in_4
  OR_7432_2in_IC or_7432_2in_ic_3 (
    .out_9(c3), .in_1(and_7408_2in_ic_3_out_9), .in_2(and_7408_2in_ic_3_out_10));  // open: out_11, out_12, out_10, in_5, in_6, in_7, in_8, in_3, in_4
  OR_7432_2in_IC or_7432_2in_ic_4 (
    .out_9(Cout), .in_1(and_7408_2in_ic_4_out_9), .in_2(and_7408_2in_ic_4_out_10));  // open: out_11, out_12, out_10, in_5, in_6, in_7, in_8, in_3, in_4

  // Notes on the sheet:
  //   C
  //   C
  //   C
  //   C
  //   C
endmodule

module lab_2 (
  input  in_1,
  input  in_2,
  input  in_3,
  input  in_4,
  input  in_5,
  input  in_6,
  input  in_7,
  input  in_8,
  input  in_9,
  input  in_10,
  input  in_11,
  output out_12,
  output out_13,
  output out_14,
  output out_15,
  output COUT
);

  wire inverter_7404_2in_ic_1_out_7, inverter_7404_2in_ic_1_out_8, inverter_7404_2in_ic_1_out_9,
       inverter_7404_2in_ic_1_out_12, x_dual_4x1_mux_1_out_11, x_dual_4x1_mux_1_out_12,
       x_dual_4x1_mux_2_out_11, x_dual_4x1_mux_2_out_12, zero;

  Inverter_7404_2in_IC inverter_7404_2in_ic_1 (
    .out_9(inverter_7404_2in_ic_1_out_9), .out_10(zero), .out_12(inverter_7404_2in_ic_1_out_12),
    .out_7(inverter_7404_2in_ic_1_out_7), .out_8(inverter_7404_2in_ic_1_out_8), .in_6(in_6), .in_1(in_9),
    .in_2(in_8), .in_3(in_7), .in_4(1'b1));  // open: out_11, in_5
  x_dual_4x1_mux x_dual_4x1_mux_1 (
    .out_12(x_dual_4x1_mux_1_out_12), .out_11(x_dual_4x1_mux_1_out_11), .in_7(zero), .in_1(in_7),
    .in_2(inverter_7404_2in_ic_1_out_9), .in_3(zero), .in_4(1'b1), .in_5(in_6),
    .in_6(inverter_7404_2in_ic_1_out_12), .in_8(1'b1), .in_9(in_11), .in_10(in_10));
  x_dual_4x1_mux x_dual_4x1_mux_2 (
    .out_12(x_dual_4x1_mux_2_out_12), .out_11(x_dual_4x1_mux_2_out_11), .in_7(zero), .in_1(in_9),
    .in_2(inverter_7404_2in_ic_1_out_7), .in_3(zero), .in_4(1'b1), .in_5(in_8),
    .in_6(inverter_7404_2in_ic_1_out_8), .in_8(1'b1), .in_9(in_11), .in_10(in_10));
  four_bit_adder four_bit_adder_1 (
    .D0(out_15), .D1(out_14), .D2(out_13), .D3(out_12), .Cout(COUT), .A_4(in_2),
    .B_4(x_dual_4x1_mux_1_out_12), .B(x_dual_4x1_mux_2_out_11), .C(in_1), .A(in_5), .A_2(in_4),
    .B_2(x_dual_4x1_mux_2_out_12), .A_3(in_3), .B_3(x_dual_4x1_mux_1_out_11));

  // Other names for the same wires on the sheet: A1 = in_5; A2 = in_4; A3 = in_3; A4 = in_2; B1 = in_9; B2 = in_8;
  //   B3 = in_7; B4 = in_6; Ci = in_1; D0 = out_15; D1 = out_14; D2 = out_13; D3 = out_12; S0 = in_11; S1 = in_10
endmodule

module lab_3 (
  input  A4,
  input  A3,
  input  A2,
  input  A1,
  input  B4,
  input  B3,
  input  B2,
  input  B1,
  output S8,
  output S7,
  output S6,
  output S5,
  output S4,
  output S3,
  output S2,
  output S1
);

  wire A1B2, A1B3, A1B4, A2B1, A2B2, A2B3, A2B4, A3B1, A3B2, A3B3, A3B4, A4B1, A4B2, A4B3, A4B4,
       four_bit_adder_1_cout, four_bit_adder_1_d1, four_bit_adder_1_d2, four_bit_adder_1_d3,
       four_bit_adder_2_cout, four_bit_adder_2_d1, four_bit_adder_2_d2, four_bit_adder_2_d3;

  AND_7408_2in_IC and_7408_2in_ic_1 (
    .out_11(A1B3), .out_12(A1B4), .out_10(A1B2), .out_9(S1), .in_5(A1), .in_6(B3), .in_7(A1), .in_8(B4),
    .in_1(B1), .in_2(A1), .in_3(B2), .in_4(A1));
  AND_7408_2in_IC and_7408_2in_ic_2 (
    .out_11(A2B4), .out_12(A2B3), .out_10(A2B2), .out_9(A2B1), .in_5(A2), .in_6(B4), .in_7(A2), .in_8(B3),
    .in_1(B1), .in_2(A2), .in_3(B2), .in_4(A2));
  AND_7408_2in_IC and_7408_2in_ic_3 (
    .out_11(A3B3), .out_12(A3B4), .out_10(A3B2), .out_9(A3B1), .in_5(A3), .in_6(B3), .in_7(A3), .in_8(B4),
    .in_1(A3), .in_2(B1), .in_3(A3), .in_4(B2));
  AND_7408_2in_IC and_7408_2in_ic_4 (
    .out_11(A4B3), .out_12(A4B4), .out_10(A4B2), .out_9(A4B1), .in_5(A4), .in_6(B3), .in_7(A4), .in_8(B4),
    .in_1(A4), .in_2(B1), .in_3(A4), .in_4(B2));
  four_bit_adder four_bit_adder_1 (
    .D0(S2), .D1(four_bit_adder_1_d1), .D2(four_bit_adder_1_d2), .D3(four_bit_adder_1_d3),
    .Cout(four_bit_adder_1_cout), .A_4(A2B4), .B_4(1'b0), .B(A2B1), .C(1'b0), .A(A1B2), .A_2(A1B3),
    .B_2(A2B2), .A_3(A2B3), .B_3(A1B4));
  four_bit_adder four_bit_adder_2 (
    .D0(S3), .D1(four_bit_adder_2_d1), .D2(four_bit_adder_2_d2), .D3(four_bit_adder_2_d3),
    .Cout(four_bit_adder_2_cout), .A_4(A3B4), .B_4(four_bit_adder_1_cout), .B(four_bit_adder_1_d1), .C(1'b0),
    .A(A3B1), .A_2(A3B2), .B_2(four_bit_adder_1_d2), .A_3(A3B3), .B_3(four_bit_adder_1_d3));
  four_bit_adder four_bit_adder_3 (
    .D0(S4), .D1(S5), .D2(S6), .D3(S7), .Cout(S8), .A_4(A4B4), .B_4(four_bit_adder_2_cout),
    .B(four_bit_adder_2_d1), .C(1'b0), .A(A4B1), .A_2(A4B2), .B_2(four_bit_adder_2_d2), .A_3(A4B3),
    .B_3(four_bit_adder_2_d3));

  // Other names for the same wires on the sheet: A1B1 = S1
endmodule

module Register_16_bit (
  input  [15:0] in_1,
  input  in_2,
  input  [3:0] in_3,
  input  [3:0] in_4,
  input  in_5,
  input  [3:0] in_6,
  output [15:0] out_7,
  output [15:0] out_8
);

  wire demultiplexer_1_out0, demultiplexer_1_out1, demultiplexer_1_out2, demultiplexer_1_out3,
       demultiplexer_1_out4, demultiplexer_1_out5, demultiplexer_1_out6, demultiplexer_1_out7,
       demultiplexer_1_out8, demultiplexer_1_out9, demultiplexer_1_out10, demultiplexer_1_out11,
       demultiplexer_1_out12, demultiplexer_1_out13, demultiplexer_1_out14, demultiplexer_1_out15;
  wire [15:0] R0_q, R1_q, R2_q, R3_q, R4_q, R5_q, R6_q, R7_q, R8_q, R9_q, R10_q, R11_q, R12_q, R13_q, R14_q,
       R15_q;

  Demultiplexer #(.select(4)) demultiplexer_1 (
    .out0(demultiplexer_1_out0), .out1(demultiplexer_1_out1), .out2(demultiplexer_1_out2),
    .out3(demultiplexer_1_out3), .out4(demultiplexer_1_out4), .out5(demultiplexer_1_out5),
    .out6(demultiplexer_1_out6), .out7(demultiplexer_1_out7), .out8(demultiplexer_1_out8),
    .out9(demultiplexer_1_out9), .out10(demultiplexer_1_out10), .out11(demultiplexer_1_out11),
    .out12(demultiplexer_1_out12), .out13(demultiplexer_1_out13), .out14(demultiplexer_1_out14),
    .out15(demultiplexer_1_out15), .in(in_2), .sel(in_4));
  Register #(.width(16)) R0 (.D(in_1), .en(demultiplexer_1_out0), .Q(R0_q), .clk(in_5));  // open: clr
  Register #(.width(16)) R1 (.D(in_1), .en(demultiplexer_1_out1), .Q(R1_q), .clk(in_5));  // open: clr
  Register #(.width(16)) R2 (.D(in_1), .en(demultiplexer_1_out2), .Q(R2_q), .clk(in_5));  // open: clr
  Register #(.width(16)) R3 (.D(in_1), .en(demultiplexer_1_out3), .Q(R3_q), .clk(in_5));  // open: clr
  Register #(.width(16)) R4 (.D(in_1), .en(demultiplexer_1_out4), .Q(R4_q), .clk(in_5));  // open: clr
  Register #(.width(16)) R5 (.D(in_1), .en(demultiplexer_1_out5), .Q(R5_q), .clk(in_5));  // open: clr
  Register #(.width(16)) R6 (.D(in_1), .en(demultiplexer_1_out6), .Q(R6_q), .clk(in_5));  // open: clr
  Register #(.width(16)) R7 (.D(in_1), .en(demultiplexer_1_out7), .Q(R7_q), .clk(in_5));  // open: clr
  Register #(.width(16)) R8 (.D(in_1), .en(demultiplexer_1_out8), .Q(R8_q), .clk(in_5));  // open: clr
  Register #(.width(16)) R9 (.D(in_1), .en(demultiplexer_1_out9), .Q(R9_q), .clk(in_5));  // open: clr
  Register #(.width(16)) R10 (.D(in_1), .en(demultiplexer_1_out10), .Q(R10_q), .clk(in_5));  // open: clr
  Register #(.width(16)) R11 (.D(in_1), .en(demultiplexer_1_out11), .Q(R11_q), .clk(in_5));  // open: clr
  Register #(.width(16)) R12 (.D(in_1), .en(demultiplexer_1_out12), .Q(R12_q), .clk(in_5));  // open: clr
  Register #(.width(16)) R13 (.D(in_1), .en(demultiplexer_1_out13), .Q(R13_q), .clk(in_5));  // open: clr
  Register #(.width(16)) R14 (.D(in_1), .en(demultiplexer_1_out14), .Q(R14_q), .clk(in_5));  // open: clr
  Register #(.width(16)) R15 (.D(in_1), .en(demultiplexer_1_out15), .Q(R15_q), .clk(in_5));  // open: clr
  Multiplexer #(.select(4), .width(16)) multiplexer_1 (
    .in0(R0_q), .in1(R1_q), .in2(R2_q), .in3(R3_q), .in4(R4_q), .in5(R5_q), .in6(R6_q), .in7(R7_q),
    .in8(R8_q), .in9(R9_q), .in10(R10_q), .in11(R11_q), .in12(R12_q), .in13(R13_q), .in14(R14_q),
    .in15(R15_q), .out(out_7), .sel(in_3));
  Multiplexer #(.select(4), .width(16)) multiplexer_2 (
    .in0(R0_q), .in1(R1_q), .in2(R2_q), .in3(R3_q), .in4(R4_q), .in5(R5_q), .in6(R6_q), .in7(R7_q),
    .in8(R8_q), .in9(R9_q), .in10(R10_q), .in11(R11_q), .in12(R12_q), .in13(R13_q), .in14(R14_q),
    .in15(R15_q), .out(out_8), .sel(in_6));
endmodule

module lab_five (
  input  in_1,
  input  in_2,
  input  [15:0] in_3,
  input  in_4,
  input  [2:0] in_5,
  output [3:0] Opcode,
  output [3:0] Rs,
  output [3:0] Rt,
  output [3:0] Rd,
  output [15:0] out_10,
  output [15:0] out_11,
  output [15:0] out_12,
  output out_13
);

  wire clock_1_out;
  wire [15:0] adder_1_out, PC_q;

  Register #(.width(16)) PC (.D(adder_1_out), .Q(PC_q), .clk(clock_1_out));  // open: en, clr
  ROM #(.addrWidth(16), .dataWidth(16)) rom_1 (.addr(PC_q), .data({Opcode, Rs, Rt, Rd}));
  Adder #(.width(16)) adder_1 (.a(PC_q), .b(16'h1), .out(adder_1_out));  // open: cin, cout
  Clock clock_1 (.out(clock_1_out));
  Register_16_bit register_16_bit_1 (
    .out_8(out_10), .out_7(out_11), .in_2(in_4), .in_6(Rt), .in_3(Rs), .in_4(Rd), .in_1(out_12),
    .in_5(clock_1_out));
  ALU_16_Bit alu_16_bit_1 (
    .out_7(out_12), .out_8(out_13), .in_5(out_10), .in_4(out_11), .in_3(in_5), .in_2(in_1), .in_1(in_2));  // open: out_6

  // Notes on the sheet:
  //   contents of rom_1 (hex, n*v repeats v):
  //   234 123 34a 1324
  //   0000 0010 0011 0100
endmodule

module ALU_1_BIt (
  input  in_1,
  input  in_2,
  input  in_3,
  input  [2:0] in_4,
  input  in_5,
  output out_6,
  output out_7
);

  wire adder_1_out, and_1_out, multiplexer_1_out, nand_1_out, nor_1_out, not_1_out, or_1_out, xor_1_out;

  not not_1 (not_1_out, in_3);
  Multiplexer multiplexer_1 (.in0(in_3), .in1(not_1_out), .out(multiplexer_1_out), .sel(in_5));
  Adder #(.width(1)) adder_1 (.a(in_2), .b(multiplexer_1_out), .out(adder_1_out), .cin(in_1), .cout(out_6));
  and and_1 (and_1_out, in_2, in_3);
  or or_1 (or_1_out, in_2, in_3);
  xor xor_1 (xor_1_out, in_2, in_3);
  nand nand_1 (nand_1_out, in_2, in_3);
  nor nor_1 (nor_1_out, in_2, in_3);
  Multiplexer #(.select(3)) multiplexer_2 (
    .in0(adder_1_out), .in1(nor_1_out), .in2(and_1_out), .in3(or_1_out), .in4(xor_1_out), .in5(nand_1_out),
    .out(out_7), .sel(in_4));  // open: in6, in7
endmodule

module ALU_16_Bit (
  input  in_1,
  input  in_2,
  input  [2:0] in_3,
  input  [15:0] in_4,
  input  [15:0] in_5,
  output out_6,
  output [15:0] out_7,
  output out_8
);

  wire alu_1_bit_1_out_6, alu_1_bit_2_out_6, alu_1_bit_3_out_6, alu_1_bit_4_out_6, alu_1_bit_5_out_6,
       alu_1_bit_6_out_6, alu_1_bit_7_out_6, alu_1_bit_8_out_6, alu_1_bit_9_out_6, alu_1_bit_10_out_6,
       alu_1_bit_11_out_6, alu_1_bit_12_out_6, alu_1_bit_13_out_6, alu_1_bit_14_out_6, alu_1_bit_15_out_6;
  wire [2:0] undriven;

  ALU_1_BIt alu_1_bit_1 (
    .out_6(alu_1_bit_1_out_6), .out_7(out_7[0]), .in_3(in_5[0]), .in_2(in_4[0]), .in_1(in_1), .in_5(in_2),
    .in_4(in_3));
  ALU_1_BIt alu_1_bit_2 (
    .out_6(alu_1_bit_2_out_6), .out_7(out_7[1]), .in_3(in_5[1]), .in_2(in_4[1]), .in_1(alu_1_bit_1_out_6),
    .in_5(in_2), .in_4(in_3));
  ALU_1_BIt alu_1_bit_3 (
    .out_6(alu_1_bit_3_out_6), .out_7(out_7[2]), .in_3(in_5[2]), .in_2(in_4[2]), .in_1(alu_1_bit_2_out_6),
    .in_5(in_2), .in_4(in_3));
  ALU_1_BIt alu_1_bit_4 (
    .out_6(alu_1_bit_4_out_6), .out_7(out_7[3]), .in_3(in_5[3]), .in_2(in_4[3]), .in_1(alu_1_bit_3_out_6),
    .in_5(in_2), .in_4(in_3));
  ALU_1_BIt alu_1_bit_5 (
    .out_6(alu_1_bit_5_out_6), .out_7(out_7[4]), .in_3(in_5[4]), .in_2(in_4[4]), .in_1(alu_1_bit_4_out_6),
    .in_5(in_2), .in_4(in_3));
  ALU_1_BIt alu_1_bit_6 (
    .out_6(alu_1_bit_6_out_6), .out_7(out_7[5]), .in_3(in_5[5]), .in_2(in_4[5]), .in_1(alu_1_bit_5_out_6),
    .in_5(in_2), .in_4(in_3));
  ALU_1_BIt alu_1_bit_7 (
    .out_6(alu_1_bit_7_out_6), .out_7(out_7[6]), .in_3(in_5[6]), .in_2(in_4[6]), .in_1(alu_1_bit_6_out_6),
    .in_5(in_2), .in_4(in_3));
  ALU_1_BIt alu_1_bit_8 (
    .out_6(alu_1_bit_8_out_6), .out_7(out_7[7]), .in_3(in_5[7]), .in_2(in_4[7]), .in_1(alu_1_bit_7_out_6),
    .in_5(in_2), .in_4(undriven));
  ALU_1_BIt alu_1_bit_9 (
    .out_6(alu_1_bit_9_out_6), .out_7(out_7[8]), .in_3(in_5[8]), .in_2(in_4[8]), .in_1(alu_1_bit_8_out_6),
    .in_5(in_2), .in_4(undriven));
  ALU_1_BIt alu_1_bit_10 (
    .out_6(alu_1_bit_10_out_6), .out_7(out_7[9]), .in_3(in_5[9]), .in_2(in_4[9]), .in_1(alu_1_bit_9_out_6),
    .in_5(in_2), .in_4(undriven));
  ALU_1_BIt alu_1_bit_11 (
    .out_6(alu_1_bit_11_out_6), .out_7(out_7[10]), .in_3(in_5[10]), .in_2(in_4[10]),
    .in_1(alu_1_bit_10_out_6), .in_5(in_2), .in_4(undriven));
  ALU_1_BIt alu_1_bit_12 (
    .out_6(alu_1_bit_12_out_6), .out_7(out_7[11]), .in_3(in_5[11]), .in_2(in_4[11]),
    .in_1(alu_1_bit_11_out_6), .in_5(in_2), .in_4(undriven));
  ALU_1_BIt alu_1_bit_13 (
    .out_6(alu_1_bit_13_out_6), .out_7(out_7[12]), .in_3(in_5[12]), .in_2(in_4[12]),
    .in_1(alu_1_bit_12_out_6), .in_5(in_2), .in_4(undriven));
  ALU_1_BIt alu_1_bit_14 (
    .out_6(alu_1_bit_14_out_6), .out_7(out_7[13]), .in_3(in_5[13]), .in_2(in_4[13]),
    .in_1(alu_1_bit_13_out_6), .in_5(in_2), .in_4(undriven));
  ALU_1_BIt alu_1_bit_15 (
    .out_6(alu_1_bit_15_out_6), .out_7(out_7[14]), .in_3(in_5[14]), .in_2(in_4[14]),
    .in_1(alu_1_bit_14_out_6), .in_5(in_2), .in_4(undriven));
  ALU_1_BIt alu_1_bit_16 (
    .out_6(out_8), .out_7(out_7[15]), .in_3(in_5[15]), .in_2(in_4[15]), .in_1(alu_1_bit_15_out_6),
    .in_5(in_2), .in_4(undriven));
  nor nor_1 (out_6, out_7[0], out_7[1], out_7[2], out_7[3], out_7[4], out_7[5], out_7[6], out_7[7], out_7[9], out_7[10], out_7[11], out_7[12], out_7[13], out_7[14], out_7[15], out_7[8]);
endmodule

module I_type (
  input  in_1,
  input  in_2,
  input  [15:0] in_3,
  input  in_4,
  input  [2:0] in_5,
  output [3:0] Opcode,
  output [3:0] Rs,
  output [3:0] Rt,
  output [3:0] imm,
  output [15:0] out_10,
  output [15:0] out_11,
  output [15:0] out_12,
  output out_13
);

  wire clock_1_out;
  wire [3:0] undriven;
  wire [15:0] adder_1_out, PC_q;

  Register #(.width(16)) PC (.D(adder_1_out), .Q(PC_q), .clk(clock_1_out));  // open: en, clr
  ROM #(.addrWidth(16), .dataWidth(16)) rom_1 (.addr(PC_q), .data({Opcode, Rs, Rt, imm}));
  Adder #(.width(16)) adder_1 (.a(PC_q), .b(16'h1), .out(adder_1_out));  // open: cin, cout
  Clock clock_1 (.out(clock_1_out));
  Register_16_bit register_16_bit_1 (
    .out_7(out_11), .in_2(in_4), .in_6(undriven), .in_3(Rs), .in_4(Rt), .in_1(out_12), .in_5(clock_1_out));  // open: out_8
  assign out_10 = {{12{1'b0}}, imm};  // Bit_Extender bit_extender_1
  ALU_16_Bit alu_16_bit_1 (
    .out_7(out_12), .out_8(out_13), .in_5(out_10), .in_4(out_11), .in_3(in_5), .in_2(in_1), .in_1(in_2));  // open: out_6

  // Notes on the sheet:
  //   contents of rom_1 (hex, n*v repeats v):
  //   234 123 34a 1324
  //   0000 0010 0011 0100
endmodule

module load_type (
  input  in_1,
  input  in_2,
  input  [15:0] in_3,
  input  in_4,
  input  [2:0] in_5,
  input  load_eb,
  input  in_7,
  output [3:0] rt_dest,
  output [3:0] Rs_base_reg,
  output [3:0] Opcode,
  output [3:0] imm,
  output [15:0] out_12,
  output [15:0] out_13,
  output [15:0] out_14,
  output out_15
);

  wire clock_1_out;
  wire [15:0] adder_1_out, PC_q, ram_1_dout, register_16_bit_1_out_8;

  Register #(.width(16)) PC (.D(adder_1_out), .Q(PC_q), .clk(clock_1_out));  // open: en, clr
  ROM #(.addrWidth(16), .dataWidth(16)) rom_1 (.addr(PC_q), .data({Opcode, Rs_base_reg, rt_dest, imm}));
  Adder #(.width(16)) adder_1 (.a(PC_q), .b(16'h1), .out(adder_1_out));  // open: cin, cout
  Clock clock_1 (.out(clock_1_out));
  Register_16_bit register_16_bit_1 (
    .out_8(register_16_bit_1_out_8), .out_7(out_13), .in_2(in_4), .in_3(Rs_base_reg), .in_4(rt_dest),
    .in_1(ram_1_dout), .in_5(clock_1_out));  // open: in_6
  assign out_12 = {{12{1'b0}}, imm};  // Bit_Extender bit_extender_1
  ALU_16_Bit alu_16_bit_1 (
    .out_7(out_14), .out_8(out_15), .in_5(out_12), .in_4(out_13), .in_3(in_5), .in_2(in_1), .in_1(in_2));  // open: out_6
  RAM #(.addrWidth(16), .asyncread("true"), .dataWidth(16), .\type ("nonvolatile")) ram_1 (
    .addr(out_14), .we(in_7), .oe(load_eb), .clk(clock_1_out), .dout(ram_1_dout));  // open: din

  // Notes on the sheet:
  //   Opp | Rs | Rd| Offset
  //   contents of rom_1 (hex, n*v repeats v):
  //   2525 123 34a 1324
  //   Lw $r5, $r2, 5
  //   0010
  //   2
  //   r2 = mem [r5+5]
  //   0000 0010 0011 0100
  //   0101 0010 0101
  //   5      2    5
endmodule

module store_type (
  input  in_1,
  input  in_2,
  input  [15:0] in_3,
  input  in_4,
  input  [2:0] in_5,
  input  load_eb,
  input  in_7,
  output [3:0] rt_dest,
  output [3:0] Rs_base_reg,
  output [3:0] Opcode,
  output [3:0] imm,
  output [15:0] out_12,
  output [15:0] out_13,
  output [15:0] out_14,
  output out_15
);

  wire clock_1_out;
  wire [15:0] adder_1_out, PC_q, register_16_bit_1_out_8;

  ROM #(.addrWidth(16), .dataWidth(16)) rom_1 (.addr(PC_q), .data({Opcode, Rs_base_reg, rt_dest, imm}));
  Register #(.width(16)) PC (.D(adder_1_out), .Q(PC_q), .clk(clock_1_out));  // open: en, clr
  Adder #(.width(16)) adder_1 (.a(PC_q), .b(16'h1), .out(adder_1_out));  // open: cin, cout
  Clock clock_1 (.out(clock_1_out));
  Register_16_bit register_16_bit_1 (
    .out_8(register_16_bit_1_out_8), .out_7(out_13), .in_2(in_4), .in_6(rt_dest), .in_3(Rs_base_reg),
    .in_5(clock_1_out));  // open: in_4, in_1
  assign out_12 = {{12{1'b0}}, imm};  // Bit_Extender bit_extender_1
  ALU_16_Bit alu_16_bit_1 (
    .out_7(out_14), .out_8(out_15), .in_5(out_12), .in_4(out_13), .in_3(in_5), .in_2(in_1), .in_1(in_2));  // open: out_6
  RAM #(.addrWidth(16), .dataWidth(16), .\type ("nonvolatile")) ram_1 (
    .addr(out_14), .we(in_7), .oe(load_eb), .clk(clock_1_out), .din(register_16_bit_1_out_8));  // open: dout

  // Notes on the sheet:
  //   Opp | Rs | Rd| Offset
  //   contents of rom_1 (hex, n*v repeats v):
  //   2525 123 34a 1324
  //   opp rs rt imm
  //   sw $r5, $r2, 5
  //   0010
  //   2
  //   mem [r5+5] = r2
  //   0000 0010 0011 0100
  //   0101 0010 0101
  //   5      2    5
endmodule

module lab_7_assignment (
  input  Jump,
  input  reg_dest_itype,
  input  write_eb_1,
  input  [2:0] ALU_OP,
  input  ALU_sr_itype,
  input  [15:0] in_6,
  input  sub,
  input  load_eb,
  input  store_eb,
  input  RAM_to_Reg,
  output [3:0] rd_imm,
  output [3:0] Opcode,
  output [3:0] Rs,
  output [3:0] Rt,
  output [15:0] data_2,
  output [15:0] data_1,
  output [15:0] out_17,
  output out_18
);

  wire clock_1_out;
  wire [3:0] multiplexer_2_out;
  wire [11:0] adder_1_out_2;
  wire [15:0] bit_extender_1_out, multiplexer_1_out, multiplexer_4_out, PC_q, ram_1_dout,
       register_16_bit_1_out_8;
  wire [15:12] adder_1_out;

  Multiplexer #(.width(16)) multiplexer_1 (
    .in0({adder_1_out, adder_1_out_2}), .in1({adder_1_out, Rs, Rt, rd_imm}), .out(multiplexer_1_out),
    .sel(Jump));
  ROM #(.addrWidth(16), .dataWidth(16)) rom_1 (.addr(PC_q), .data({Opcode, Rs, Rt, rd_imm}));
  Register #(.width(16)) PC (.D(multiplexer_1_out), .Q(PC_q), .clk(clock_1_out));  // open: en, clr
  Adder #(.width(16)) adder_1 (.a(PC_q), .b(16'h1), .out({adder_1_out, adder_1_out_2}));  // open: cin, cout
  Clock clock_1 (.out(clock_1_out));
  Multiplexer #(.width(4)) multiplexer_2 (.in0(rd_imm), .in1(Rt), .out(multiplexer_2_out), .sel(reg_dest_itype));
  Register_16_bit register_16_bit_1 (
    .out_8(register_16_bit_1_out_8), .out_7(data_1), .in_2(write_eb_1), .in_6(Rt), .in_3(Rs),
    .in_4(multiplexer_2_out), .in_1(multiplexer_4_out), .in_5(clock_1_out));
  assign bit_extender_1_out = {{12{rd_imm[3]}}, rd_imm};  // Bit_Extender bit_extender_1
  Multiplexer #(.width(16)) multiplexer_3 (
    .in0(register_16_bit_1_out_8), .in1(bit_extender_1_out), .out(data_2), .sel(ALU_sr_itype));
  ALU_16_Bit alu_16_bit_1 (
    .out_7(out_17), .out_8(out_18), .in_5(data_2), .in_4(data_1), .in_3(ALU_OP), .in_2(sub), .in_1(sub));  // open: out_6
  RAM #(.addrWidth(16), .asyncread("true"), .dataWidth(16), .\type ("nonvolatile")) ram_1 (
    .addr(out_17), .we(store_eb), .oe(load_eb), .clk(clock_1_out), .din(register_16_bit_1_out_8),
    .dout(ram_1_dout));
  Multiplexer #(.width(16)) multiplexer_4 (.in0(out_17), .in1(ram_1_dout), .out(multiplexer_4_out), .sel(RAM_to_Reg));

  // Notes on the sheet:
  //   contents of rom_1 (hex, n*v repeats v):
  //   123 1126 4124 900a 81*0 9003 173*0 9003 21581*0 9003
  //   ADD $R1 $R2 $R3
  //   0000  0001  0010 0011
  //   0          1          2       3
  //   R3 = R1 + R2 
  //   ADDi $R1 $R2 6
  //   0001 0001 0010 0101
  //   1          1          2       6
  //   R2 = R1 + 6
  //   LW $R1 $R2 4
  //   0100  0001  0010 0100
  //   4          1          2       4
  //   R2 = mem [4+R1]
  //   SW $R1 $R2  3
  //   0101 0001 0100 0010
  //   5          1          2       3
  //    mem [3+R1] = R2
endmodule

module CU (
  input  [3:0] Opp,
  output Rd_dst,
  output reg_write_eb,
  output ALU_src,
  output [2:0] ALU_OP,
  output Sub,
  output Lw,
  output sw,
  output mem_to_reg,
  output jump
);

  wire and_1_out, and_2_out, and_3_out, and_4_out, and_5_out, and_6_out, and_7_out, and_8_out, and_9_out,
       and_10_out, and_11_out, and_12_out, and_13_out, and_14_out, not_1_out, not_2_out, not_3_out, not_4_out;

  not not_1 (not_1_out, Opp[3]);
  not not_2 (not_2_out, Opp[2]);
  not not_3 (not_3_out, Opp[1]);
  not not_4 (not_4_out, Opp[0]);
  and and_1 (and_1_out, not_1_out, Opp[1], not_4_out);
  and and_2 (and_2_out, not_1_out, Opp[2], Opp[1]);
  and and_3 (and_3_out, Opp[3], not_2_out, not_3_out);
  and and_4 (and_4_out, not_1_out, not_4_out);
  and and_5 (and_5_out, not_2_out, not_3_out);
  and and_6 (and_6_out, not_1_out, Opp[2]);
  and and_7 (and_7_out, not_1_out, Opp[1]);
  and and_8 (and_8_out, Opp[3], not_2_out, not_3_out);
  and and_9 (and_9_out, not_1_out, Opp[2], not_3_out);
  and and_10 (and_10_out, Opp[3], not_2_out, not_3_out);
  and and_11 (and_11_out, not_1_out, Opp[2], not_3_out, Opp[0]);
  and and_12 (and_12_out, Opp[3], not_2_out, not_3_out, not_4_out);
  and and_13 (and_13_out, not_1_out, not_2_out, not_3_out, Opp[0]);
  and and_14 (and_14_out, not_1_out, Opp[2], Opp[1], Opp[0]);
  and and_15 (Lw, not_1_out, not_2_out, Opp[1], not_4_out);
  and and_16 (sw, not_1_out, not_2_out, Opp[1], Opp[0]);
  and and_17 (mem_to_reg, not_1_out, not_2_out, Opp[1], not_4_out);
  and and_18 (jump, Opp[3], not_2_out, Opp[1], not_4_out);
  or or_1 (Rd_dst, and_1_out, and_2_out, and_3_out);
  or or_2 (reg_write_eb, and_4_out, and_5_out, and_6_out);
  or or_3 (ALU_src, and_7_out, and_8_out);
  or or_4 (ALU_OP[1], and_9_out, and_10_out);
  or or_5 (ALU_OP[0], and_11_out, and_12_out);
  or or_6 (Sub, and_13_out, and_14_out);

  assign ALU_OP[2] = 1'b0;
endmodule

module datapath_with_CU (
  input  [15:0] in_1,
  output [3:0] rd_imm,
  output [3:0] Opcode,
  output [3:0] Rs,
  output [3:0] Rt,
  output [15:0] data_2,
  output [15:0] data_1,
  output [15:0] out_8,
  output out_9
);

  wire clock_1_out, cu_1_alu_src, cu_1_jump, cu_1_lw, cu_1_mem_to_reg, cu_1_rd_dst, cu_1_reg_write_eb,
       cu_1_sub, cu_1_sw;
  wire [2:0] cu_1_alu_op;
  wire [3:0] adder_1_out, adder_1_out_2, adder_1_out_3, adder_1_out_4, multiplexer_2_out;
  wire [15:0] bit_extender_1_out, multiplexer_1_out, multiplexer_4_out, PC_q, ram_1_dout,
       register_16_bit_1_out_8;

  CU cu_1 (
    .reg_write_eb(cu_1_reg_write_eb), .ALU_src(cu_1_alu_src), .ALU_OP(cu_1_alu_op), .Sub(cu_1_sub),
    .Lw(cu_1_lw), .sw(cu_1_sw), .mem_to_reg(cu_1_mem_to_reg), .jump(cu_1_jump), .Rd_dst(cu_1_rd_dst),
    .Opp(Opcode));
  Multiplexer #(.width(16)) multiplexer_1 (
    .in0({adder_1_out, adder_1_out_4, adder_1_out_3, adder_1_out_2}), .in1({adder_1_out, Rs, Rt, rd_imm}),
    .out(multiplexer_1_out), .sel(cu_1_jump));
  ROM #(.addrWidth(16), .dataWidth(16)) rom_1 (.addr(PC_q), .data({Opcode, Rs, Rt, rd_imm}));
  Register #(.width(16)) PC (.D(multiplexer_1_out), .Q(PC_q), .clk(clock_1_out));  // open: en, clr
  Adder #(.width(16)) adder_1 (
    .a(PC_q), .b(16'h1), .out({adder_1_out, adder_1_out_4, adder_1_out_3, adder_1_out_2}));  // open: cin, cout
  Clock clock_1 (.out(clock_1_out));
  Multiplexer #(.width(4)) multiplexer_2 (.in0(rd_imm), .in1(Rt), .out(multiplexer_2_out), .sel(cu_1_rd_dst));
  Register_16_bit register_16_bit_1 (
    .out_8(register_16_bit_1_out_8), .out_7(data_1), .in_2(cu_1_reg_write_eb), .in_6(Rt), .in_3(Rs),
    .in_4(multiplexer_2_out), .in_1(multiplexer_4_out), .in_5(clock_1_out));
  assign bit_extender_1_out = {{12{rd_imm[3]}}, rd_imm};  // Bit_Extender bit_extender_1
  Multiplexer #(.width(16)) multiplexer_3 (
    .in0(register_16_bit_1_out_8), .in1(bit_extender_1_out), .out(data_2), .sel(cu_1_alu_src));
  ALU_16_Bit alu_16_bit_1 (
    .out_7(out_8), .out_8(out_9), .in_5(data_2), .in_4(data_1), .in_3(cu_1_alu_op), .in_2(cu_1_sub),
    .in_1(cu_1_sub));  // open: out_6
  RAM #(.addrWidth(16), .asyncread("true"), .dataWidth(16), .\type ("nonvolatile")) ram_1 (
    .addr(out_8), .we(cu_1_sw), .oe(cu_1_lw), .clk(clock_1_out), .din(register_16_bit_1_out_8),
    .dout(ram_1_dout));
  Multiplexer #(.width(16)) multiplexer_4 (
    .in0(out_8), .in1(ram_1_dout), .out(multiplexer_4_out), .sel(cu_1_mem_to_reg));

  // Notes on the sheet:
  //   contents of rom_1 (hex, n*v repeats v):
  //   2124 1126 4124 900a a002 80*0 9003 173*0 9003 21581*0 9003
  //   ADD $R1 $R2 $R3
  //   0000  0001  0010 0011
  //   0          1          2       3
  //   R3 = R1 + R2 
  //   ADDi $R1 $R2 6
  //   0001 0001 0010 0101
  //   1          1          2       6
  //   R2 = R1 + 6
  //   LW $R1 $R2 4
  //   0010  0001  0010 0100
  //   2          1          2       4
  //   R2 = mem [4+R1]
  //   SW $R1 $R2  3
  //   0101 0001 0100 0010
  //   5          1          2       3
  //    mem [3+R1] = R2
endmodule
