// Logisim project project.circ as structural Verilog: 6 circuits, main circuit main
module main (
  input  [9:0] in_1,
  output [9:0] out_2,
  output [3:0] OP,
  output [2:0] RS_RD,
  output [9:0] RD_RS,
  output [2:0] RT,
  output [9:0] RT_IMM,
  output overf,
  output Co
);

  wire beqz, bgtz, Bi, bltz, br, branch_ic_1_out_6, clock_1_out, cu_1_alu_src_imm, cu_1_keybo, cu_1_ld,
       cu_1_reg_write_eb, cu_1_st, cu_1_t0slct, j, ot, sign, zero;
  wire [1:0] cu_1_alu_op;
  wire [2:0] multiplexer_1_out, multiplexer_2_out, multiplexer_3_out;
  wire [3:0] one, three, two;
  wire [7:3] rom_1_data;
  wire [9:0] adder_1_out, adder_2_out, adder_3_out, bit_extender_1_out, imm, multiplexer_4_out,
       multiplexer_5_out, multiplexer_6_out, multiplexer_8_out, PC_q, ram_1_dout, register_10_bit_1_out_8;
  wire [9:8] controlled_buffer_1_out;

  Hex_Digit_Display #(.decimalPoint("false")) hex_digit_display_1 (.value(three));
  Hex_Digit_Display #(.decimalPoint("false")) hex_digit_display_2 (.value(two));
  Hex_Digit_Display #(.decimalPoint("false")) hex_digit_display_3 (.value(one));
  Clock clock_1 (.out(clock_1_out));
  Register #(.width(10)) PC (.D(multiplexer_6_out), .Q(PC_q), .clk(clock_1_out));  // open: en, clr
  CU cu_1 (
    .ST(cu_1_st), .LD(cu_1_ld), .J(j), .ALU_OP(cu_1_alu_op), .reg_write_eb(cu_1_reg_write_eb),
    .T0Slct(cu_1_t0slct), .branch(br), .Beqz(beqz), .Bgtz(bgtz), .Bltz(bltz), .Bi(Bi), .ot(ot),
    .keybo(cu_1_keybo), .ALU_SRC_IMM(cu_1_alu_src_imm), .OP(OP));
  ROM #(.addrWidth(10), .dataWidth(12)) rom_1 (.addr(PC_q), .data({OP, rom_1_data[7], RS_RD, rom_1_data[3], RT}));
  Adder #(.width(10)) adder_1 (.a(10'h1), .b(PC_q), .out(adder_1_out));  // open: cin, cout
  Multiplexer #(.width(3)) multiplexer_1 (.in0(RT), .in1(3'b101), .out(multiplexer_1_out), .sel(cu_1_t0slct));
  Multiplexer #(.width(3)) multiplexer_2 (.in0(RS_RD), .in1(3'b101), .out(multiplexer_2_out), .sel(cu_1_t0slct));
  Adder #(.width(10)) adder_2 (.a(adder_1_out), .b(bit_extender_1_out), .out(adder_2_out));  // open: cin, cout
  assign bit_extender_1_out = {{4{RS_RD[2]}}, {RS_RD, RT}};  // Bit_Extender bit_extender_1
  Multiplexer #(.width(3)) multiplexer_3 (
    .in0(multiplexer_2_out), .in1(multiplexer_1_out), .out(multiplexer_3_out), .sel(cu_1_keybo));
  Multiplexer #(.width(10)) multiplexer_4 (
    .in0(multiplexer_8_out), .in1(in_1), .out(multiplexer_4_out), .sel(cu_1_keybo));
  Multiplexer #(.width(10)) multiplexer_5 (.in0(adder_1_out), .in1(adder_2_out), .out(multiplexer_5_out), .sel(j));
  register_10_bit register_10_bit_1 (
    .out_8(register_10_bit_1_out_8), .out_7(RD_RS), .in_3(RS_RD), .in_6(multiplexer_1_out),
    .in_1(multiplexer_4_out), .in_2(cu_1_reg_write_eb), .in_4(multiplexer_3_out), .in_5(clock_1_out));
  Adder #(.width(10)) adder_3 (.a(adder_1_out), .b(imm), .out(adder_3_out));  // open: cin, cout
  assign imm = {{7{RT[2]}}, RT};  // Bit_Extender bit_extender_2
  Multiplexer #(.width(10)) multiplexer_6 (
    .in0(multiplexer_5_out), .in1(adder_3_out), .out(multiplexer_6_out), .sel(branch_ic_1_out_6));
  Multiplexer #(.width(10)) multiplexer_7 (
    .in0(register_10_bit_1_out_8), .in1(imm), .out(RT_IMM), .sel(cu_1_alu_src_imm));
  ALU_10_bit alu_10_bit_1 (
    .sign(sign), .R(out_2), .Zero(zero), .ovf(overf), .Co(Co), .B(RT_IMM), .ALU_OP(cu_1_alu_op), .A(RD_RS),
    .Ci(Bi), .Bi(Bi), .in_1(br));
  branch_IC branch_ic_1 (.out_6(branch_ic_1_out_6), .sign(sign), .bgtz(bgtz), .bltz(bltz), .zero(zero), .beqz(beqz));
  Multiplexer #(.width(10)) multiplexer_8 (.in0(out_2), .in1(ram_1_dout), .out(multiplexer_8_out), .sel(cu_1_ld));
  RAM #(.addrWidth(10), .asyncread("true"), .dataWidth(10), .\type ("nonvolatile")) ram_1 (
    .addr(out_2), .we(cu_1_st), .oe(cu_1_ld), .clk(clock_1_out), .din(register_10_bit_1_out_8),
    .dout(ram_1_dout));
  assign {controlled_buffer_1_out, two, one} = ot ? RT_IMM : 10'bz;  // Controlled_Buffer controlled_buffer_1
  assign three = {{2{1'b0}}, controlled_buffer_1_out};  // Bit_Extender bit_extender_3

  // Other names for the same wires on the sheet: Keyboard[9:0] = in_1

  // Notes on the sheet:
  //   -512 to 511
  //   Beqz $s0 2
  //   s0 == 0 -> 2
  //   001   010 
  //   0101
  //   1
  //   5
  //   2
  //   Bgtz $s0 -2
  //   s0>0? -> -2
  //   010
  //   0110
  //   6
  //   1
  //   ADD 
  //   0000 
  //   0
  //   (1)110
  //   e
  //   5 - 3
  //   9 - 6
  //   OP            RS/RD           RT 
  //   7
  //   2 - 0
  //   $S1
  //   $S2
  //   010 
  //   2
  //   Bltz $s2 -3
  //   s2<0? -> -3
  //   011
  //   0111
  //   3
  //   011
  //   3
  //   (1)101
  //   d
  //   contents of rom_1 (hex, n*v repeats v):
  //   23 22d 313 423 a02 843 0 512 61e 73d 82d 943 e02 f02
  //   For load
  //   store
  //   9 - 6
  //   0010
  //   2
  //   Bnez $s1 -3
  //   s1!=0? -> -3
  //   010
  //   1000
  //   8
  //   2
  //   5 - 3
  //   ADDi      $S1       -3
  //   $S1            =          $S1  +    -3
  //   2
  //   (1)101
  //   d
  //   2 - 0
  //   010 
  //   (1)101
  //   d
  //   1001
  //   9
  //   bgez   $s3    3
  //   s3 > = 0 -> 3
  //   100
  //   100
  //   4
  //   3
  //   9 - 6
  //   5 - 3
  //   LW    $S0     3
  //   $t0 = mem [3+$S0]
  //   0011  001 100
  //   3          1      3
  //   2 - 0
  //   4
  //   SW    $S1  3
  //   mem [3+$S1] = $t0
  //   1000  010 100
  //   3
  //   2
  //   1010
  //   a
  //   00 = AND
  //   01 = OR 
  //   10 = ADD
  //   11 = NOR
  //   J      2
  //   000010
  //   2
endmodule

module register_10_bit (
  input  [9:0] in_1,
  input  in_2,
  input  [2:0] in_3,
  input  [2:0] in_4,
  input  in_5,
  input  [2:0] in_6,
  output [9:0] out_7,
  output [9:0] out_8
);

  wire demultiplexer_1_out1, demultiplexer_1_out2, demultiplexer_1_out3, demultiplexer_1_out4,
       demultiplexer_1_out5, demultiplexer_1_out6, demultiplexer_1_out7;
  wire [9:0] S0_001_q, S1_010_q, S2_011_q, S3_100_q, T0_101_q, T1_110_q, T2_111_q, zero_000_q;

  Demultiplexer #(.select(3)) demultiplexer_1 (
    .out1(demultiplexer_1_out1), .out2(demultiplexer_1_out2), .out3(demultiplexer_1_out3),
    .out4(demultiplexer_1_out4), .out5(demultiplexer_1_out5), .out6(demultiplexer_1_out6),
    .out7(demultiplexer_1_out7), .in(in_2), .sel(in_4));  // open: out0
  Register #(.width(10)) zero_000 (.D({10{1'b0}}), .Q(zero_000_q));  // open: en, clk, clr
  Register #(.width(10)) S0_001 (.D(in_1), .en(demultiplexer_1_out1), .Q(S0_001_q), .clk(in_5));  // open: clr
  Register #(.width(10)) S1_010 (.D(in_1), .en(demultiplexer_1_out2), .Q(S1_010_q), .clk(in_5));  // open: clr
  Register #(.width(10)) S2_011 (.D(in_1), .en(demultiplexer_1_out3), .Q(S2_011_q), .clk(in_5));  // open: clr
  Register #(.width(10)) S3_100 (.D(in_1), .en(demultiplexer_1_out4), .Q(S3_100_q), .clk(in_5));  // open: clr
  Register #(.width(10)) T0_101 (.D(in_1), .en(demultiplexer_1_out5), .Q(T0_101_q), .clk(in_5));  // open: clr
  Register #(.width(10)) T1_110 (.D(in_1), .en(demultiplexer_1_out6), .Q(T1_110_q), .clk(in_5));  // open: clr
  Register #(.width(10)) T2_111 (.D(in_1), .en(demultiplexer_1_out7), .Q(T2_111_q), .clk(in_5));  // open: clr
  Multiplexer #(.select(3), .width(10)) multiplexer_1 (
    .in0(zero_000_q), .in1(S0_001_q), .in2(S1_010_q), .in3(S2_011_q), .in4(S3_100_q), .in5(T0_101_q),
    .in6(T1_110_q), .in7(T2_111_q), .out(out_7), .sel(in_3));
  Multiplexer #(.select(3), .width(10)) multiplexer_2 (
    .in0(zero_000_q), .in1(S0_001_q), .in2(S1_010_q), .in3(S2_011_q), .in4(S3_100_q), .in5(T0_101_q),
    .in6(T1_110_q), .in7(T2_111_q), .out(out_8), .sel(in_6));
endmodule

module ALU_1_bit (
  input  Cin,
  input  A,
  input  B,
  input  [1:0] ALU_OP,
  input  branch,
  input  Bin,
  output R,
  output Cout
);

  wire adder_1_out, and_1_out, multiplexer_1_out, multiplexer_2_out, nor_1_out, not_1_out, or_1_out;

  Multiplexer multiplexer_1 (.in0(B), .in1(not_1_out), .out(multiplexer_1_out), .sel(Bin));
  not not_1 (not_1_out, B);
  Multiplexer multiplexer_2 (.in0(B), .in1(1'b1), .out(multiplexer_2_out), .sel(branch));
  and and_1 (and_1_out, A, multiplexer_2_out);
  or or_1 (or_1_out, A, B);
  Adder #(.width(1)) adder_1 (.a(A), .b(multiplexer_1_out), .out(adder_1_out), .cin(Cin), .cout(Cout));
  nor nor_1 (nor_1_out, A, B);
  Multiplexer #(.select(2)) multiplexer_3 (
    .in0(and_1_out), .in1(or_1_out), .in2(adder_1_out), .in3(nor_1_out), .out(R), .sel(ALU_OP));
endmodule

module ALU_10_bit (
  input  in_1,
  input  Ci,
  input  Bi,
  input  [1:0] ALU_OP,
  input  [9:0] A,
  input  [9:0] B,
  output ovf,
  output Co,
  output [9:0] R,
  output Zero,
  output sign
);

  wire alu_1_bit_1_cout, alu_1_bit_2_cout, alu_1_bit_3_cout, alu_1_bit_4_cout, alu_1_bit_5_cout,
       alu_1_bit_6_cout, alu_1_bit_7_cout, alu_1_bit_8_cout, alu_1_bit_9_cout;

  ALU_1_bit alu_1_bit_1 (
    .Cout(alu_1_bit_1_cout), .R(R[0]), .B(B[0]), .Cin(Ci), .Bin(Bi), .A(A[0]), .branch(in_1), .ALU_OP(ALU_OP));
  ALU_1_bit alu_1_bit_2 (
    .Cout(alu_1_bit_2_cout), .R(R[1]), .B(B[1]), .Cin(alu_1_bit_1_cout), .Bin(Bi), .A(A[1]), .branch(in_1),
    .ALU_OP(ALU_OP));
  ALU_1_bit alu_1_bit_3 (
    .Cout(alu_1_bit_3_cout), .R(R[2]), .B(B[2]), .Cin(alu_1_bit_2_cout), .Bin(Bi), .A(A[2]), .branch(in_1),
    .ALU_OP(ALU_OP));
  ALU_1_bit alu_1_bit_4 (
    .Cout(alu_1_bit_4_cout), .R(R[3]), .B(B[3]), .Cin(alu_1_bit_3_cout), .Bin(Bi), .A(A[3]), .branch(in_1),
    .ALU_OP(ALU_OP));
  ALU_1_bit alu_1_bit_5 (
    .Cout(alu_1_bit_5_cout), .R(R[4]), .B(B[4]), .Cin(alu_1_bit_4_cout), .Bin(Bi), .A(A[4]), .branch(in_1),
    .ALU_OP(ALU_OP));
  ALU_1_bit alu_1_bit_6 (
    .Cout(alu_1_bit_6_cout), .R(R[5]), .B(B[5]), .Cin(alu_1_bit_5_cout), .Bin(Bi), .A(A[5]), .branch(in_1),
    .ALU_OP(ALU_OP));
  ALU_1_bit alu_1_bit_7 (
    .Cout(alu_1_bit_7_cout), .R(R[6]), .B(B[6]), .Cin(alu_1_bit_6_cout), .Bin(Bi), .A(A[6]), .branch(in_1),
    .ALU_OP(ALU_OP));
  ALU_1_bit alu_1_bit_8 (
    .Cout(alu_1_bit_8_cout), .R(R[7]), .B(B[7]), .Cin(alu_1_bit_7_cout), .Bin(Bi), .A(A[7]), .branch(in_1),
    .ALU_OP(ALU_OP));
  ALU_1_bit alu_1_bit_9 (
    .Cout(alu_1_bit_9_cout), .R(R[8]), .B(B[8]), .Cin(alu_1_bit_8_cout), .Bin(Bi), .A(A[8]), .branch(in_1),
    .ALU_OP(ALU_OP));
  ALU_1_bit alu_1_bit_10 (
    .Cout(Co), .R(R[9]), .B(B[9]), .Cin(alu_1_bit_9_cout), .Bin(Bi), .A(A[9]), .branch(in_1), .ALU_OP(ALU_OP));
  xor xor_1 (ovf, alu_1_bit_9_cout, Co);
  nor nor_1 (Zero, R[0], R[1], R[1], R[2], R[3], R[4], R[5], R[7], R[8], R[9]);

  assign sign = R[9];

  // Other names for the same wires on the sheet: overflow = ovf
endmodule

module CU (
  input  [3:0] OP,
  output ALU_SRC_IMM,
  output ST,
  output LD,
  output J,
  output [1:0] ALU_OP,
  output reg_write_eb,
  output T0Slct,
  output branch,
  output Beqz,
  output Bgtz,
  output Bltz,
  output Bi,
  output ot,
  output keybo
);

  wire and_1_out, and_2_out, and_3_out, and_7_out, and_8_out, and_9_out, and_11_out, and_12_out, and_13_out,
       and_14_out, and_15_out, and_16_out, and_17_out, and_18_out, and_19_out, and_20_out, and_21_out,
       and_22_out, and_23_out, and_24_out, and_25_out, not_1_out, not_2_out, not_3_out, not_4_out;

  not not_1 (not_1_out, OP[3]);
  not not_2 (not_2_out, OP[2]);
  not not_3 (not_3_out, OP[1]);
  not not_4 (not_4_out, OP[0]);
  and and_1 (and_1_out, not_1_out, OP[1]);
  and and_2 (and_2_out, not_1_out, OP[2]);
  and and_3 (and_3_out, OP[3], not_2_out, not_3_out);
  and and_4 (ST, not_1_out, OP[2], not_3_out, not_4_out);
  and and_5 (LD, not_1_out, not_2_out, OP[1], OP[0]);
  and and_6 (J, OP[3], not_2_out, OP[1], not_4_out);
  and and_7 (and_7_out, not_1_out, not_2_out);
  and and_8 (and_8_out, not_1_out, not_3_out, not_4_out);
  and and_9 (and_9_out, OP[3], OP[2], not_3_out, OP[0]);
  and and_10 (ALU_OP[0], OP[3], OP[2], not_3_out);
  and and_11 (and_11_out, not_1_out, not_2_out);
  and and_12 (and_12_out, not_2_out, OP[1], OP[0]);
  and and_13 (and_13_out, OP[3], OP[2], not_3_out);
  and and_14 (and_14_out, OP[3], OP[2], not_4_out);
  and and_15 (and_15_out, not_1_out, not_2_out, OP[1], OP[0]);
  and and_16 (and_16_out, not_1_out, OP[2], not_3_out, not_4_out);
  and and_17 (and_17_out, not_1_out, OP[2], OP[0]);
  and and_18 (and_18_out, not_1_out, OP[2], OP[1]);
  and and_19 (and_19_out, OP[3], not_2_out, not_3_out);
  and and_20 (and_20_out, not_1_out, OP[2], not_3_out, OP[0]);
  and and_21 (and_21_out, OP[3], not_2_out, not_3_out, OP[0]);
  and and_22 (and_22_out, not_1_out, OP[2], OP[1], not_4_out);
  and and_23 (and_23_out, OP[3], not_2_out, not_3_out);
  and and_24 (and_24_out, not_1_out, OP[2], OP[1], OP[0]);
  and and_25 (and_25_out, OP[3], not_2_out, not_3_out, not_4_out);
  and and_26 (Bi, not_1_out, not_2_out, not_3_out, OP[0]);
  and and_27 (ot, OP[3], OP[2], OP[1], OP[0]);
  and and_28 (keybo, OP[3], OP[2], OP[1], not_4_out);
  or or_1 (ALU_SRC_IMM, and_1_out, and_2_out, and_3_out);
  or or_2 (ALU_OP[1], and_7_out, and_8_out, and_9_out);
  or or_3 (reg_write_eb, and_11_out, and_12_out, and_13_out, and_14_out);
  or or_4 (T0Slct, and_15_out, and_16_out);
  or or_5 (branch, and_17_out, and_18_out, and_19_out);
  or or_6 (Beqz, and_20_out, and_21_out);
  or or_7 (Bgtz, and_22_out, and_23_out);
  or or_8 (Bltz, and_24_out, and_25_out);
endmodule

module branch_IC (
  input  bltz,
  input  bgtz,
  input  sign,
  input  zero,
  input  beqz,
  output out_6
);

  wire and_1_out, and_2_out, and_3_out, nor_1_out, or_2_out, or_3_out;

  or or_1 (out_6, and_3_out, and_1_out, or_2_out, and_2_out, or_3_out);
  or or_2 (or_2_out, and_3_out, and_1_out);
  or or_3 (or_3_out, and_1_out, and_2_out);
  and and_1 (and_1_out, bgtz, nor_1_out);
  and and_2 (and_2_out, beqz, zero);
  and and_3 (and_3_out, bltz, sign);
  nor nor_1 (nor_1_out, zero, sign);
endmodule
