// Logisim project project_v2.circ as structural Verilog: 11 circuits, main circuit main
module main (
  input  [9:0] minus_512_to_511,
  output [9:0] out_2,
  output [3:0] OP,
  output [2:0] RS_RD,
  output [9:0] RD_RS,
  output [2:0] RT,
  output [9:0] RT_IMM,
  output overf,
  output Co
);

  wire beqz, bgtz, Bi, bltz, br, branch_ic_1_out_6, clock_1_out, cu_1_alu_src_imm, cu_1_keybo, cu_1_ld,
       cu_1_reg_write_eb, cu_1_st, cu_1_t0slct, enter_okay_out, inpt_1_out_4, inpt_out, j, l1, l2, l3, l4,
       l5, l6, l7, m1, m2, m3, m4, m5, m6, m7, n1, n2, n3, n4, n5, n6, n7, ot, seven_seg_1_a, seven_seg_1_b,
       seven_seg_1_c, seven_seg_1_d, seven_seg_1_e, seven_seg_1_f, seven_seg_1_g, seven_seg_2_a,
       seven_seg_2_b, seven_seg_2_c, seven_seg_2_d, seven_seg_2_e, seven_seg_2_f, seven_seg_2_g,
       seven_seg_3_a, seven_seg_3_b, seven_seg_3_c, seven_seg_3_d, seven_seg_3_e, seven_seg_3_f,
       seven_seg_3_g, sign, sin_bit, zero;
  wire [1:0] cu_1_alu_op;
  wire [2:0] multiplexer_1_out, multiplexer_2_out, multiplexer_3_out;
  wire [3:0] lsb, msb, n;
  wire [9:0] adder_1_out, adder_2_out, adder_3_out, bit_extender_1_out, imm, multiplexer_4_out,
       multiplexer_5_out, multiplexer_6_out, multiplexer_8_out, PC_q, ram_1_dout, register_10_bit_1_out_8;

  _7_Segment_Display u_7_segment_display_1 (.g(sin_bit));  // open: f, a, b, e, d, c, dp
  _7_Segment_Display u_7_segment_display_2 (.g(m7), .f(m6), .a(m1), .b(m2), .e(m5), .d(m4), .c(m3));  // open: dp
  Button enter_okay (.out(enter_okay_out));
  _7_Segment_Display u_7_segment_display_3 (.g(n7), .f(n6), .a(n1), .b(n2), .e(n5), .d(n4), .c(n3));  // open: dp
  Clock clock_1 (.out(clock_1_out));
  _7_Segment_Display u_7_segment_display_4 (.g(l7), .f(l6), .a(l1), .b(l2), .e(l5), .d(l4), .c(l3));  // open: dp
  inpt inpt_1 (.out_4(inpt_1_out_4), .enter(enter_okay_out), .inpt_ot(inpt_out), .clk(clock_1_out));
  Register #(.width(10)) PC (.D(multiplexer_6_out), .Q(PC_q), .clk(inpt_1_out_4));  // open: en, clr
  CU cu_1 (
    .ST(cu_1_st), .LD(cu_1_ld), .J(j), .ALU_OP(cu_1_alu_op), .reg_write_eb(cu_1_reg_write_eb),
    .T0Slct(cu_1_t0slct), .branch(br), .Beqz(beqz), .Bgtz(bgtz), .Bltz(bltz), .Bi(Bi), .ot(ot),
    .keybo(cu_1_keybo), .inpt(inpt_out), .ALU_SRC_IMM(cu_1_alu_src_imm), .OP(OP));
  ROM #(.addrWidth(10), .dataWidth(10)) rom_1 (.addr(PC_q), .data({OP, RS_RD, RT}));
  Adder #(.width(10)) adder_1 (.a(10'h1), .b(PC_q), .out(adder_1_out));  // open: cin, cout
  Multiplexer #(.width(3)) multiplexer_1 (.in0(RT), .in1(3'b101), .out(multiplexer_1_out), .sel(cu_1_t0slct));
  Multiplexer #(.width(3)) multiplexer_2 (.in0(RS_RD), .in1(3'b101), .out(multiplexer_2_out), .sel(cu_1_t0slct));
  Adder #(.width(10)) adder_2 (.a(adder_1_out), .b(bit_extender_1_out), .out(adder_2_out));  // open: cin, cout
  assign bit_extender_1_out = {{4{RS_RD[2]}}, {RS_RD, RT}};  // Bit_Extender bit_extender_1
  Multiplexer #(.width(3)) multiplexer_3 (
    .in0(multiplexer_2_out), .in1(multiplexer_1_out), .out(multiplexer_3_out), .sel(cu_1_keybo));
  Multiplexer #(.width(10)) multiplexer_4 (
    .in0(multiplexer_8_out), .in1(minus_512_to_511), .out(multiplexer_4_out), .sel(cu_1_keybo));
  Multiplexer #(.width(10)) multiplexer_5 (.in0(adder_1_out), .in1(adder_2_out), .out(multiplexer_5_out), .sel(j));
  register_10_bit register_10_bit_1 (
    .out_8(register_10_bit_1_out_8), .out_7(RD_RS), .in_3(RS_RD), .in_6(multiplexer_1_out),
    .in_1(multiplexer_4_out), .in_2(cu_1_reg_write_eb), .in_4(multiplexer_3_out), .in_5(inpt_1_out_4));
  Adder #(.width(10)) adder_3 (.a(adder_1_out), .b(imm), .out(adder_3_out));  // open: cin, cout
  assign imm = {{7{RT[2]}}, RT};  // Bit_Extender bit_extender_2
  Multiplexer #(.width(10)) multiplexer_6 (
    .in0(multiplexer_5_out), .in1(adder_3_out), .out(multiplexer_6_out), .sel(branch_ic_1_out_6));
  Multiplexer #(.width(10)) multiplexer_7 (
    .in0(register_10_bit_1_out_8), .in1(imm), .out(RT_IMM), .sel(cu_1_alu_src_imm));
  ALU_10_bit alu_10_bit_1 (
    .sign(sign), .R(out_2), .Zero(zero), .ovf(overf), .Co(Co), .B(RT_IMM), .ALU_OP(cu_1_alu_op), .A(RD_RS),
    .Ci(Bi), .Bi(Bi), .in_1(br));
  branch_IC branch_ic_1 (.out_6(branch_ic_1_out_6), .sign(sign), .bgtz(bgtz), .bltz(bltz), .zero(zero), .beqz(beqz));
  Multiplexer #(.width(10)) multiplexer_8 (.in0(out_2), .in1(ram_1_dout), .out(multiplexer_8_out), .sel(cu_1_ld));
  RAM #(.addrWidth(10), .asyncread("true"), .dataWidth(10), .\type ("nonvolatile")) ram_1 (
    .addr(out_2), .we(cu_1_st), .oe(cu_1_ld), .clk(inpt_1_out_4), .din(register_10_bit_1_out_8),
    .dout(ram_1_dout));
  assign m1 = ot ? seven_seg_1_a : 1'bz;  // Controlled_Buffer controlled_buffer_1
  assign m2 = ot ? seven_seg_1_b : 1'bz;  // Controlled_Buffer controlled_buffer_2
  assign m3 = ot ? seven_seg_1_c : 1'bz;  // Controlled_Buffer controlled_buffer_3
  assign m5 = ot ? seven_seg_1_e : 1'bz;  // Controlled_Buffer controlled_buffer_4
  assign m4 = ot ? seven_seg_1_d : 1'bz;  // Controlled_Buffer controlled_buffer_5
  assign m6 = ot ? seven_seg_1_f : 1'bz;  // Controlled_Buffer controlled_buffer_6
  seven_seg seven_seg_1 (
    .a(seven_seg_1_a), .b(seven_seg_1_b), .c(seven_seg_1_c), .d(seven_seg_1_d), .e(seven_seg_1_e),
    .f(seven_seg_1_f), .g(seven_seg_1_g), .in_1(msb));
  assign m7 = ot ? seven_seg_1_g : 1'bz;  // Controlled_Buffer controlled_buffer_7
  assign n2 = ot ? seven_seg_2_b : 1'bz;  // Controlled_Buffer controlled_buffer_8
  assign n1 = ot ? seven_seg_2_a : 1'bz;  // Controlled_Buffer controlled_buffer_9
  assign n3 = ot ? seven_seg_2_c : 1'bz;  // Controlled_Buffer controlled_buffer_10
  assign n4 = ot ? seven_seg_2_d : 1'bz;  // Controlled_Buffer controlled_buffer_11
  assign n5 = ot ? seven_seg_2_e : 1'bz;  // Controlled_Buffer controlled_buffer_12
  assign sin_bit = ot ? RT_IMM[9] : 1'bz;  // Controlled_Buffer controlled_buffer_13
  seven_seg seven_seg_2 (
    .a(seven_seg_2_a), .b(seven_seg_2_b), .c(seven_seg_2_c), .d(seven_seg_2_d), .e(seven_seg_2_e),
    .f(seven_seg_2_f), .g(seven_seg_2_g), .in_1(n));
  assign n7 = ot ? seven_seg_2_g : 1'bz;  // Controlled_Buffer controlled_buffer_14
  assign n6 = ot ? seven_seg_2_f : 1'bz;  // Controlled_Buffer controlled_buffer_15
  pass_bin pass_bin_1 (.in_1(RT_IMM[8:0]), .Sign_1(RT_IMM[9]), .lsb(lsb), .mid(n), .msb(msb));
  assign l1 = ot ? seven_seg_3_a : 1'bz;  // Controlled_Buffer controlled_buffer_16
  assign l2 = ot ? seven_seg_3_b : 1'bz;  // Controlled_Buffer controlled_buffer_17
  assign l3 = ot ? seven_seg_3_c : 1'bz;  // Controlled_Buffer controlled_buffer_18
  seven_seg seven_seg_3 (
    .a(seven_seg_3_a), .b(seven_seg_3_b), .c(seven_seg_3_c), .d(seven_seg_3_d), .e(seven_seg_3_e),
    .f(seven_seg_3_f), .g(seven_seg_3_g), .in_1(lsb));
  assign l5 = ot ? seven_seg_3_e : 1'bz;  // Controlled_Buffer controlled_buffer_19
  assign l4 = ot ? seven_seg_3_d : 1'bz;  // Controlled_Buffer controlled_buffer_20
  assign l7 = ot ? seven_seg_3_g : 1'bz;  // Controlled_Buffer controlled_buffer_21
  assign l6 = ot ? seven_seg_3_f : 1'bz;  // Controlled_Buffer controlled_buffer_22

  // Other names for the same wires on the sheet: Keyboard[9:0] = minus_512_to_511

  // Notes on the sheet:
  //   3
  //   11 1000 0010
  //   8
  //   2
  //   In $s1
  //   contents of rom_1 (hex, n*v repeats v):
  //   382 3c2
  //   For load
  //   store
  //   00 = AND
  //   01 = OR 
  //   10 = ADD
  //   11 = NOR
endmodule

module register_10_bit (
  input  [9:0] in_1,
  input  in_2,
  input  [2:0] in_3,
  input  [2:0] in_4,
  input  in_5,
  input  [2:0] in_6,
  output [9:0] out_7,
  output [9:0] out_8
);

  wire demultiplexer_1_out1, demultiplexer_1_out2, demultiplexer_1_out3, demultiplexer_1_out4,
       demultiplexer_1_out5, demultiplexer_1_out6, demultiplexer_1_out7;
  wire [9:0] S0_001_q, S1_010_q, S2_011_q, S3_100_q, T0_101_q, T1_110_q, T2_111_q, zero_000_q;

  Demultiplexer #(.select(3)) demultiplexer_1 (
    .out1(demultiplexer_1_out1), .out2(demultiplexer_1_out2), .out3(demultiplexer_1_out3),
    .out4(demultiplexer_1_out4), .out5(demultiplexer_1_out5), .out6(demultiplexer_1_out6),
    .out7(demultiplexer_1_out7), .in(in_2), .sel(in_4));  // open: out0
  Register #(.width(10)) zero_000 (.D({10{1'b0}}), .Q(zero_000_q));  // open: en, clk, clr
  Register #(.width(10)) S0_001 (.D(in_1), .en(demultiplexer_1_out1), .Q(S0_001_q), .clk(in_5));  // open: clr
  Register #(.width(10)) S1_010 (.D(in_1), .en(demultiplexer_1_out2), .Q(S1_010_q), .clk(in_5));  // open: clr
  Register #(.width(10)) S2_011 (.D(in_1), .en(demultiplexer_1_out3), .Q(S2_011_q), .clk(in_5));  // open: clr
  Register #(.width(10)) S3_100 (.D(in_1), .en(demultiplexer_1_out4), .Q(S3_100_q), .clk(in_5));  // open: clr
  Register #(.width(10)) T0_101 (.D(in_1), .en(demultiplexer_1_out5), .Q(T0_101_q), .clk(in_5));  // open: clr
  Register #(.width(10)) T1_110 (.D(in_1), .en(demultiplexer_1_out6), .Q(T1_110_q), .clk(in_5));  // open: clr
  Register #(.width(10)) T2_111 (.D(in_1), .en(demultiplexer_1_out7), .Q(T2_111_q), .clk(in_5));  // open: clr
  Multiplexer #(.select(3), .width(10)) multiplexer_1 (
    .in0(zero_000_q), .in1(S0_001_q), .in2(S1_010_q), .in3(S2_011_q), .in4(S3_100_q), .in5(T0_101_q),
    .in6(T1_110_q), .in7(T2_111_q), .out(out_7), .sel(in_3));
  Multiplexer #(.select(3), .width(10)) multiplexer_2 (
    .in0(zero_000_q), .in1(S0_001_q), .in2(S1_010_q), .in3(S2_011_q), .in4(S3_100_q), .in5(T0_101_q),
    .in6(T1_110_q), .in7(T2_111_q), .out(out_8), .sel(in_6));
endmodule

module ALU_1_bit (
  input  Cin,
  input  A,
  input  B,
  input  [1:0] ALU_OP,
  input  branch,
  input  Bin,
  output R,
  output Cout
);

  wire adder_1_out, and_1_out, multiplexer_1_out, multiplexer_2_out, nor_1_out, not_1_out, or_1_out;

  Multiplexer multiplexer_1 (.in0(B), .in1(not_1_out), .out(multiplexer_1_out), .sel(Bin));
  not not_1 (not_1_out, B);
  Multiplexer multiplexer_2 (.in0(B), .in1(1'b1), .out(multiplexer_2_out), .sel(branch));
  and and_1 (and_1_out, A, multiplexer_2_out);
  or or_1 (or_1_out, A, B);
  Adder #(.width(1)) adder_1 (.a(A), .b(multiplexer_1_out), .out(adder_1_out), .cin(Cin), .cout(Cout));
  nor nor_1 (nor_1_out, A, B);
  Multiplexer #(.select(2)) multiplexer_3 (
    .in0(and_1_out), .in1(or_1_out), .in2(adder_1_out), .in3(nor_1_out), .out(R), .sel(ALU_OP));
endmodule

module ALU_10_bit (
  input  in_1,
  input  Ci,
  input  Bi,
  input  [1:0] ALU_OP,
  input  [9:0] A,
  input  [9:0] B,
  output ovf,
  output Co,
  output [9:0] R,
  output Zero,
  output sign
);

  wire alu_1_bit_1_cout, alu_1_bit_2_cout, alu_1_bit_3_cout, alu_1_bit_4_cout, alu_1_bit_5_cout,
       alu_1_bit_6_cout, alu_1_bit_7_cout, alu_1_bit_8_cout, alu_1_bit_9_cout;

  ALU_1_bit alu_1_bit_1 (
    .Cout(alu_1_bit_1_cout), .R(R[0]), .B(B[0]), .Cin(Ci), .Bin(Bi), .A(A[0]), .branch(in_1), .ALU_OP(ALU_OP));
  ALU_1_bit alu_1_bit_2 (
    .Cout(alu_1_bit_2_cout), .R(R[1]), .B(B[1]), .Cin(alu_1_bit_1_cout), .Bin(Bi), .A(A[1]), .branch(in_1),
    .ALU_OP(ALU_OP));
  ALU_1_bit alu_1_bit_3 (
    .Cout(alu_1_bit_3_cout), .R(R[2]), .B(B[2]), .Cin(alu_1_bit_2_cout), .Bin(Bi), .A(A[2]), .branch(in_1),
    .ALU_OP(ALU_OP));
  ALU_1_bit alu_1_bit_4 (
    .Cout(alu_1_bit_4_cout), .R(R[3]), .B(B[3]), .Cin(alu_1_bit_3_cout), .Bin(Bi), .A(A[3]), .branch(in_1),
    .ALU_OP(ALU_OP));
  ALU_1_bit alu_1_bit_5 (
    .Cout(alu_1_bit_5_cout), .R(R[4]), .B(B[4]), .Cin(alu_1_bit_4_cout), .Bin(Bi), .A(A[4]), .branch(in_1),
    .ALU_OP(ALU_OP));
  ALU_1_bit alu_1_bit_6 (
    .Cout(alu_1_bit_6_cout), .R(R[5]), .B(B[5]), .Cin(alu_1_bit_5_cout), .Bin(Bi), .A(A[5]), .branch(in_1),
    .ALU_OP(ALU_OP));
  ALU_1_bit alu_1_bit_7 (
    .Cout(alu_1_bit_7_cout), .R(R[6]), .B(B[6]), .Cin(alu_1_bit_6_cout), .Bin(Bi), .A(A[6]), .branch(in_1),
    .ALU_OP(ALU_OP));
  ALU_1_bit alu_1_bit_8 (
    .Cout(alu_1_bit_8_cout), .R(R[7]), .B(B[7]), .Cin(alu_1_bit_7_cout), .Bin(Bi), .A(A[7]), .branch(in_1),
    .ALU_OP(ALU_OP));
  ALU_1_bit alu_1_bit_9 (
    .Cout(alu_1_bit_9_cout), .R(R[8]), .B(B[8]), .Cin(alu_1_bit_8_cout), .Bin(Bi), .A(A[8]), .branch(in_1),
    .ALU_OP(ALU_OP));
  ALU_1_bit alu_1_bit_10 (
    .Cout(Co), .R(R[9]), .B(B[9]), .Cin(alu_1_bit_9_cout), .Bin(Bi), .A(A[9]), .branch(in_1), .ALU_OP(ALU_OP));
  xor xor_1 (ovf, alu_1_bit_9_cout, Co);
  nor nor_1 (Zero, R[0], R[1], R[1], R[2], R[3], R[4], R[5], R[7], R[8], R[9]);

  assign sign = R[9];

  // Other names for the same wires on the sheet: overflow = ovf
endmodule

module CU (
  input  [3:0] OP,
  output ALU_SRC_IMM,
  output ST,
  output LD,
  output J,
  output [1:0] ALU_OP,
  output reg_write_eb,
  output T0Slct,
  output branch,
  output Beqz,
  output Bgtz,
  output Bltz,
  output Bi,
  output ot,
  output keybo,
  output inpt
);

  wire and_1_out, and_2_out, and_3_out, and_7_out, and_8_out, and_9_out, and_11_out, and_12_out, and_13_out,
       and_14_out, and_15_out, and_16_out, and_17_out, and_18_out, and_19_out, and_20_out, and_21_out,
       and_22_out, and_23_out, and_24_out, and_25_out, not_1_out, not_2_out, not_3_out, not_4_out;

  not not_1 (not_1_out, OP[3]);
  not not_2 (not_2_out, OP[2]);
  not not_3 (not_3_out, OP[1]);
  not not_4 (not_4_out, OP[0]);
  and and_1 (and_1_out, not_1_out, OP[1]);
  and and_2 (and_2_out, not_1_out, OP[2]);
  and and_3 (and_3_out, OP[3], not_2_out, not_3_out);
  and and_4 (ST, not_1_out, OP[2], not_3_out, not_4_out);
  and and_5 (LD, not_1_out, not_2_out, OP[1], OP[0]);
  and and_6 (J, OP[3], not_2_out, OP[1], not_4_out);
  and and_7 (and_7_out, not_1_out, not_2_out);
  and and_8 (and_8_out, not_1_out, not_3_out, not_4_out);
  and and_9 (and_9_out, OP[3], OP[2], not_3_out, OP[0]);
  and and_10 (ALU_OP[0], OP[3], OP[2], not_3_out);
  and and_11 (and_11_out, not_1_out, not_2_out);
  and and_12 (and_12_out, not_2_out, OP[1], OP[0]);
  and and_13 (and_13_out, OP[3], OP[2], not_3_out);
  and and_14 (and_14_out, OP[3], OP[2], not_4_out);
  and and_15 (and_15_out, not_1_out, not_2_out, OP[1], OP[0]);
  and and_16 (and_16_out, not_1_out, OP[2], not_3_out, not_4_out);
  and and_17 (and_17_out, not_1_out, OP[2], OP[0]);
  and and_18 (and_18_out, not_1_out, OP[2], OP[1]);
  and and_19 (and_19_out, OP[3], not_2_out, not_3_out);
  and and_20 (and_20_out, not_1_out, OP[2], not_3_out, OP[0]);
  and and_21 (and_21_out, OP[3], not_2_out, not_3_out, OP[0]);
  and and_22 (and_22_out, not_1_out, OP[2], OP[1], not_4_out);
  and and_23 (and_23_out, OP[3], not_2_out, not_3_out);
  and and_24 (and_24_out, not_1_out, OP[2], OP[1], OP[0]);
  and and_25 (and_25_out, OP[3], not_2_out, not_3_out, not_4_out);
  and and_26 (Bi, not_1_out, not_2_out, not_3_out, OP[0]);
  and and_27 (ot, OP[3], OP[2], OP[1], OP[0]);
  and and_28 (keybo, OP[3], OP[2], OP[1], not_4_out);
  and and_29 (inpt, OP[3], OP[2], OP[1]);
  or or_1 (ALU_SRC_IMM, and_1_out, and_2_out, and_3_out);
  or or_2 (ALU_OP[1], and_7_out, and_8_out, and_9_out);
  or or_3 (reg_write_eb, and_11_out, and_12_out, and_13_out, and_14_out);
  or or_4 (T0Slct, and_15_out, and_16_out);
  or or_5 (branch, and_17_out, and_18_out, and_19_out);
  or or_6 (Beqz, and_20_out, and_21_out);
  or or_7 (Bgtz, and_22_out, and_23_out);
  or or_8 (Bltz, and_24_out, and_25_out);
endmodule

module branch_IC (
  input  bltz,
  input  bgtz,
  input  sign,
  input  zero,
  input  beqz,
  output out_6
);

  wire and_1_out, and_2_out, and_3_out, nor_1_out, or_2_out, or_3_out;

  or or_1 (out_6, and_3_out, and_1_out, or_2_out, and_2_out, or_3_out);
  or or_2 (or_2_out, and_3_out, and_1_out);
  or or_3 (or_3_out, and_1_out, and_2_out);
  and and_1 (and_1_out, bgtz, nor_1_out);
  and and_2 (and_2_out, beqz, zero);
  and and_3 (and_3_out, bltz, sign);
  nor nor_1 (nor_1_out, zero, sign);
endmodule

module inpt (
  input  clk,
  input  inpt_ot,
  input  enter,
  output out_4
);

  wire and_1_out, and_2_out, not_1_out;

  not not_1 (not_1_out, inpt_ot);
  and and_1 (and_1_out, clk, not_1_out);
  and and_2 (and_2_out, enter, inpt_ot);
  or or_1 (out_4, and_1_out, and_2_out);
endmodule

module test (
  input  [9:0] minus_512_to_511,
  output [9:0] out_2,
  output [3:0] OP,
  output [2:0] RS_RD,
  output [9:0] RD_RS,
  output [2:0] RT,
  output [9:0] RT_IMM,
  output overf,
  output Co
);

  wire beqz, bgtz, Bi, bltz, br, branch_ic_1_out_6, clock_1_out, cu_1_alu_src_imm, cu_1_keybo, cu_1_ld,
       cu_1_reg_write_eb, cu_1_st, cu_1_t0slct, enter_okay_out, inpt_1_out_4, inpt_out, j, ot, sign, zero;
  wire [1:0] cu_1_alu_op;
  wire [2:0] multiplexer_1_out, multiplexer_2_out, multiplexer_3_out;
  wire [3:0] one, three, two;
  wire [9:0] adder_1_out, adder_2_out, adder_3_out, bit_extender_1_out, imm, multiplexer_4_out,
       multiplexer_5_out, multiplexer_6_out, multiplexer_8_out, PC_q, ram_1_dout, register_10_bit_1_out_8;
  wire [9:8] controlled_buffer_1_out;

  Hex_Digit_Display #(.decimalPoint("false")) hex_digit_display_1 (.value(three));
  TTY tty_1 ();  // open: data, clk, we, clr
  Hex_Digit_Display #(.decimalPoint("false")) hex_digit_display_2 (.value(two));
  Button enter_okay (.out(enter_okay_out));
  Hex_Digit_Display #(.decimalPoint("false")) hex_digit_display_3 (.value(one));
  Clock clock_1 (.out(clock_1_out));
  _7_Segment_Display u_7_segment_display_1 ();  // open: g, f, a, b, e, d, c, dp
  inpt inpt_1 (.out_4(inpt_1_out_4), .enter(enter_okay_out), .inpt_ot(inpt_out), .clk(clock_1_out));
  Register #(.width(10)) PC (.D(multiplexer_6_out), .Q(PC_q), .clk(inpt_1_out_4));  // open: en, clr
  CU cu_1 (
    .ST(cu_1_st), .LD(cu_1_ld), .J(j), .ALU_OP(cu_1_alu_op), .reg_write_eb(cu_1_reg_write_eb),
    .T0Slct(cu_1_t0slct), .branch(br), .Beqz(beqz), .Bgtz(bgtz), .Bltz(bltz), .Bi(Bi), .ot(ot),
    .keybo(cu_1_keybo), .inpt(inpt_out), .ALU_SRC_IMM(cu_1_alu_src_imm), .OP(OP));
  ROM #(.addrWidth(10), .dataWidth(10)) rom_1 (.addr(PC_q), .data({OP, RS_RD, RT}));
  Adder #(.width(10)) adder_1 (.a(10'h1), .b(PC_q), .out(adder_1_out));  // open: cin, cout
  Multiplexer #(.width(3)) multiplexer_1 (.in0(RT), .in1(3'b101), .out(multiplexer_1_out), .sel(cu_1_t0slct));
  Multiplexer #(.width(3)) multiplexer_2 (.in0(RS_RD), .in1(3'b101), .out(multiplexer_2_out), .sel(cu_1_t0slct));
  Adder #(.width(10)) adder_2 (.a(adder_1_out), .b(bit_extender_1_out), .out(adder_2_out));  // open: cin, cout
  assign bit_extender_1_out = {{4{RS_RD[2]}}, {RS_RD, RT}};  // Bit_Extender bit_extender_1
  Multiplexer #(.width(3)) multiplexer_3 (
    .in0(multiplexer_2_out), .in1(multiplexer_1_out), .out(multiplexer_3_out), .sel(cu_1_keybo));
  Multiplexer #(.width(10)) multiplexer_4 (
    .in0(multiplexer_8_out), .in1(minus_512_to_511), .out(multiplexer_4_out), .sel(cu_1_keybo));
  Multiplexer #(.width(10)) multiplexer_5 (.in0(adder_1_out), .in1(adder_2_out), .out(multiplexer_5_out), .sel(j));
  register_10_bit register_10_bit_1 (
    .out_8(register_10_bit_1_out_8), .out_7(RD_RS), .in_3(RS_RD), .in_6(multiplexer_1_out),
    .in_1(multiplexer_4_out), .in_2(cu_1_reg_write_eb), .in_4(multiplexer_3_out), .in_5(inpt_1_out_4));
  Adder #(.width(10)) adder_3 (.a(adder_1_out), .b(imm), .out(adder_3_out));  // open: cin, cout
  assign imm = {{7{RT[2]}}, RT};  // Bit_Extender bit_extender_2
  Multiplexer #(.width(10)) multiplexer_6 (
    .in0(multiplexer_5_out), .in1(adder_3_out), .out(multiplexer_6_out), .sel(branch_ic_1_out_6));
  Multiplexer #(.width(10)) multiplexer_7 (
    .in0(register_10_bit_1_out_8), .in1(imm), .out(RT_IMM), .sel(cu_1_alu_src_imm));
  ALU_10_bit alu_10_bit_1 (
    .sign(sign), .R(out_2), .Zero(zero), .ovf(overf), .Co(Co), .B(RT_IMM), .ALU_OP(cu_1_alu_op), .A(RD_RS),
    .Ci(Bi), .Bi(Bi), .in_1(br));
  branch_IC branch_ic_1 (.out_6(branch_ic_1_out_6), .sign(sign), .bgtz(bgtz), .bltz(bltz), .zero(zero), .beqz(beqz));
  Multiplexer #(.width(10)) multiplexer_8 (.in0(out_2), .in1(ram_1_dout), .out(multiplexer_8_out), .sel(cu_1_ld));
  RAM #(.addrWidth(10), .asyncread("true"), .dataWidth(10), .\type ("nonvolatile")) ram_1 (
    .addr(out_2), .we(cu_1_st), .oe(cu_1_ld), .clk(inpt_1_out_4), .din(register_10_bit_1_out_8),
    .dout(ram_1_dout));
  assign {controlled_buffer_1_out, two, one} = ot ? RT_IMM : 10'bz;  // Controlled_Buffer controlled_buffer_1
  assign three = {{2{1'b0}}, controlled_buffer_1_out};  // Bit_Extender bit_extender_3

  // Other names for the same wires on the sheet: Keyboard[9:0] = minus_512_to_511

  // Notes on the sheet:
  //   3
  //   Beqz $s0 2
  //   s0 == 0 -> 2
  //   001   010 
  //   0101
  //   1
  //   5
  //   out $s0
  //   11 1100 0001
  //   c
  //   1
  //   2
  //   Bgtz $s0 -2
  //   s0>0? -> -2
  //   010
  //   0110
  //   6
  //   1
  //   3
  //   ADD 
  //   0000 
  //   0
  //   (1)110
  //   e
  //   In $s0
  //   11 1000 0001
  //   1
  //   8
  //   5 - 3
  //   9 - 6
  //   OP            RS/RD           RT 
  //   7
  //   2 - 0
  //   $S1
  //   $S2
  //   010 
  //   2
  //   Bltz $s2 -3
  //   s2<0? -> -3
  //   011
  //   0111
  //   3
  //   011
  //   3
  //   (1)101
  //   d
  //   contents of rom_1 (hex, n*v repeats v):
  //   23 22d 313 23 202 43 0 112 21e 33d 2d 143 202 302 381 3c1
  //   For load
  //   store
  //   9 - 6
  //   0010
  //   2
  //   Bnez $s1 -3
  //   s1!=0? -> -3
  //   010
  //   1000
  //   8
  //   2
  //   5 - 3
  //   ADDi      $S1       -3
  //   $S1            =          $S1  +    -3
  //   2
  //   (1)101
  //   d
  //   2 - 0
  //   010 
  //   (1)101
  //   d
  //   1001
  //   9
  //   bgez   $s3    3
  //   s3 > = 0 -> 3
  //   100
  //   100
  //   4
  //   3
  //   9 - 6
  //   5 - 3
  //   LW    $S0     3
  //   $t0 = mem [3+$S0]
  //   0011  001 100
  //   3          1      3
  //   2 - 0
  //   4
  //   SW    $S1  3
  //   mem [3+$S1] = $t0
  //   1000  010 100
  //   3
  //   2
  //   1010
  //   a
  //   00 = AND
  //   01 = OR 
  //   10 = ADD
  //   11 = NOR
  //   J      2
  //   000010
  //   2
endmodule

module bin_bcd_9bits (
  input  B8,
  input  B7,
  input  B6,
  input  B5,
  input  B4,
  input  B3,
  input  B2,
  input  B1,
  input  B0,
  output [11:0] out_10
);

  wire and_1_out, and_2_out, and_3_out, and_4_out, and_5_out, and_6_out, and_7_out, and_8_out, and_9_out,
       and_10_out, and_11_out, and_12_out, and_13_out, and_14_out, and_15_out, and_16_out, and_17_out,
       and_18_out, and_19_out, and_20_out, and_21_out, and_22_out, and_23_out, and_24_out, and_25_out,
       and_26_out, and_27_out, and_28_out, and_29_out, and_30_out, and_31_out, and_32_out, and_33_out,
       and_34_out, and_35_out, and_36_out, and_37_out, and_38_out, and_39_out, and_40_out, and_41_out,
       and_42_out, and_43_out, and_44_out, and_45_out, and_46_out, and_47_out, and_48_out, and_49_out,
       and_50_out, and_51_out, and_52_out, and_53_out, and_54_out, and_55_out, and_56_out, and_57_out,
       and_58_out, and_59_out, and_60_out, and_61_out, and_62_out, and_63_out, and_64_out, and_65_out,
       and_66_out, and_67_out, and_68_out, and_69_out, and_70_out, and_71_out, and_72_out, and_73_out,
       and_74_out, and_75_out, and_76_out, and_77_out, and_78_out, and_79_out, and_80_out, and_81_out,
       and_82_out, and_83_out, and_84_out, and_85_out, and_86_out, and_87_out, and_88_out, and_89_out,
       and_90_out, and_91_out, and_92_out, and_93_out, and_94_out, and_95_out, and_96_out, and_97_out,
       and_98_out, and_99_out, and_100_out, and_101_out, and_102_out, and_103_out, and_104_out, and_105_out,
       and_106_out, and_107_out, and_108_out, and_109_out, and_110_out, and_111_out, and_112_out,
       and_113_out, and_114_out, and_115_out, and_116_out, and_117_out, and_118_out, and_119_out,
       and_120_out, and_121_out, and_122_out, and_123_out, and_124_out, and_125_out, and_126_out,
       and_127_out, and_128_out, and_129_out, and_130_out, and_131_out, and_132_out, and_133_out,
       and_134_out, and_135_out, and_136_out, and_137_out, and_138_out, and_139_out, and_140_out,
       and_141_out, and_142_out, and_143_out, and_144_out, and_145_out, and_146_out, and_147_out,
       and_148_out, and_149_out, and_150_out, and_151_out, and_152_out, and_153_out, and_154_out,
       and_155_out, and_156_out, and_157_out, and_158_out, and_159_out, and_160_out, and_161_out,
       and_162_out, and_163_out, and_164_out, and_165_out, and_166_out, and_167_out, and_168_out,
       and_169_out, and_170_out, and_171_out, and_172_out, and_173_out, and_174_out, and_175_out,
       and_176_out, and_177_out, and_178_out, and_179_out, and_180_out, and_181_out, and_182_out,
       and_183_out, and_184_out, and_185_out, and_186_out, and_187_out, and_188_out, and_189_out,
       and_190_out, and_191_out, and_192_out, and_193_out, and_194_out, and_195_out, and_196_out,
       and_197_out, and_198_out, and_199_out, and_200_out, and_201_out, and_202_out, and_203_out,
       and_204_out, and_205_out, and_206_out, and_207_out, and_208_out, and_209_out, and_210_out,
       and_211_out, and_212_out, and_213_out, and_214_out, and_215_out, and_216_out, and_217_out,
       and_218_out, and_219_out, and_220_out, and_221_out, and_222_out, and_223_out, and_224_out,
       and_225_out, and_226_out, and_227_out, and_228_out, and_229_out, and_230_out, and_231_out,
       and_232_out, and_233_out, and_234_out, and_235_out, and_236_out, and_237_out, and_238_out,
       and_239_out, and_240_out, and_241_out, and_242_out, and_243_out, and_244_out, and_245_out,
       and_246_out, and_247_out, and_248_out, and_249_out, and_250_out, and_251_out, and_252_out,
       and_253_out, and_254_out, and_255_out, and_256_out, and_257_out, and_258_out, and_259_out,
       and_260_out, and_261_out, and_262_out, and_263_out, and_264_out, and_265_out, and_266_out,
       and_267_out, and_268_out, and_269_out, and_270_out, and_271_out, and_272_out, and_273_out,
       and_274_out, and_275_out, and_276_out, and_277_out, and_278_out, and_279_out, and_280_out,
       and_281_out, and_282_out, and_283_out, and_284_out, and_285_out, and_286_out, and_287_out,
       and_288_out, and_289_out, and_290_out, and_291_out, and_292_out, and_293_out, and_294_out,
       and_295_out, and_296_out, and_297_out, and_298_out, and_299_out, and_300_out, and_301_out,
       and_302_out, and_303_out, and_304_out, and_305_out, and_306_out, and_307_out, and_308_out,
       and_309_out, and_310_out, and_311_out, and_312_out, and_313_out, and_314_out, and_315_out,
       and_316_out, and_317_out, and_318_out, and_319_out, and_320_out, and_321_out, and_322_out,
       and_323_out, and_324_out, and_325_out, and_326_out, and_327_out, and_328_out, and_329_out,
       and_330_out, and_331_out, and_332_out, and_333_out, and_334_out, and_335_out, and_336_out, not_1_out,
       not_2_out, not_3_out, not_4_out, not_5_out, not_6_out, not_7_out, not_8_out, or_8_out, or_9_out,
       or_10_out, or_11_out;

  not not_1 (not_1_out, B8);
  not not_2 (not_2_out, B7);
  not not_3 (not_3_out, B6);
  not not_4 (not_4_out, B5);
  not not_5 (not_5_out, B4);
  not not_6 (not_6_out, B3);
  not not_7 (not_7_out, B2);
  not not_8 (not_8_out, B1);
  and and_1 (and_1_out, B8, B7, B4);
  and and_2 (and_2_out, B8, B7, B5);
  or or_1 (out_10[10], and_1_out, and_2_out, and_3_out);
  and and_3 (and_3_out, B8, B7, B6);
  and and_4 (and_4_out, not_1_out, B7, B6, B3);
  and and_5 (and_5_out, not_1_out, B7, B6, B4);
  and and_6 (and_6_out, not_1_out, B7, B6, B5);
  and and_7 (and_7_out, B8, not_2_out);
  and and_8 (and_8_out, B8, not_3_out, not_4_out, not_5_out);
  and and_9 (and_9_out, not_2_out, B6, B5, B2);
  and and_10 (and_10_out, not_2_out, B6, B5, B3);
  and and_11 (and_11_out, not_2_out, B6, B5, B4);
  and and_12 (and_12_out, not_1_out, B7, not_3_out);
  and and_13 (and_13_out, not_1_out, B7, not_4_out, not_5_out, not_6_out);
  and and_14 (and_14_out, B7, not_3_out, not_4_out, not_5_out);
  and and_15 (and_15_out, B8, not_2_out, B5, B3, B2);
  and and_16 (and_16_out, B8, not_2_out, B5, B4);
  and and_17 (and_17_out, B8, not_2_out, B6);
  and and_18 (and_18_out, B8, B6, B5, B4, B2);
  and and_19 (and_19_out, B8, B6, B5, B4, B3);
  and and_20 (and_20_out, not_1_out, not_2_out, B6, not_4_out, B4);
  and and_21 (and_21_out, not_1_out, not_2_out, B6, B5, not_5_out, not_6_out, not_7_out);
  and and_22 (and_22_out, not_1_out, B7, not_3_out, B5, B4, B2);
  and and_23 (and_23_out, not_1_out, B7, not_3_out, B5, B4, B3);
  and and_24 (and_24_out, not_1_out, B7, B6, not_4_out, not_5_out, not_6_out);
  and and_25 (and_25_out, B8, not_2_out, not_3_out, not_4_out, B4, B3);
  and and_26 (and_26_out, B8, not_2_out, not_3_out, B5, not_5_out, not_6_out);
  and and_27 (and_27_out, B8, not_2_out, not_3_out, B5, not_5_out, not_7_out);
  and and_28 (and_28_out, B8, not_2_out, B6, B5, B4, B3, B2);
  and and_29 (and_29_out, B8, B7, not_3_out, not_4_out, not_5_out);
  and and_30 (and_30_out, B8, B7, B6, B5, not_5_out);
  and and_31 (and_31_out, B8, B7, B6, B5, not_6_out, not_7_out);
  and and_32 (and_32_out, not_1_out, not_3_out, B5, not_5_out, B3);
  and and_33 (and_33_out, not_1_out, not_2_out, not_3_out, B5, B4);
  and and_34 (and_34_out, not_1_out, not_2_out, B6, not_4_out, not_5_out);
  and and_35 (and_35_out, not_1_out, B7, not_3_out, not_4_out, B3, B2);
  and and_36 (and_36_out, not_1_out, B7, not_3_out, not_4_out, B4);
  and and_37 (and_37_out, not_1_out, B7, not_3_out, B5, not_5_out);
  and and_38 (and_38_out, not_1_out, B7, not_3_out, B5, not_6_out, not_7_out);
  and and_39 (and_39_out, not_1_out, B7, B6, B5, B4);
  and and_40 (and_40_out, B8, not_2_out, not_3_out, not_4_out, not_5_out);
  and and_41 (and_41_out, B8, not_2_out, not_3_out, not_4_out, not_6_out);
  and and_42 (and_42_out, B8, not_2_out, B6, B4, not_6_out, B2);
  and and_43 (and_43_out, B8, B6, not_4_out, B4, B3);
  and and_44 (and_44_out, B8, not_2_out, B6, B5, not_5_out);
  and and_45 (and_45_out, B8, not_2_out, B6, B5, not_7_out);
  and and_46 (and_46_out, B8, B7, not_3_out, B5, B4, B3);
  and and_47 (and_47_out, B8, B7, B6, not_4_out);
  and and_48 (and_48_out, not_2_out, not_3_out, not_4_out, B4, not_6_out, B2);
  and and_49 (and_49_out, not_1_out, not_2_out, not_3_out, not_4_out, B4, B3);
  and and_50 (and_50_out, not_1_out, not_2_out, not_3_out, B4, B3, B2);
  and and_51 (and_51_out, not_1_out, not_3_out, B5, not_5_out, not_6_out);
  and and_52 (and_52_out, not_2_out, B6, not_4_out, not_5_out);
  and and_53 (and_53_out, not_1_out, not_2_out, B6, B5, B4, B3);
  and and_54 (and_54_out, not_1_out, B7, not_3_out, not_5_out, not_6_out);
  and and_55 (and_55_out, not_1_out, B7, not_3_out, not_5_out, not_7_out);
  and and_56 (and_56_out, not_1_out, B7, B5, not_5_out);
  and and_57 (and_57_out, B7, not_3_out, B5, not_5_out, B3);
  and and_58 (and_58_out, B7, not_3_out, B5, B4, not_6_out, not_7_out);
  and and_59 (and_59_out, B7, B6, not_4_out, B4, B3, B2);
  and and_60 (and_60_out, B8, not_2_out, not_4_out, not_5_out, B2);
  and and_61 (and_61_out, B8, not_2_out, not_4_out, not_5_out, B3);
  and and_62 (and_62_out, B8, not_2_out, not_4_out, B4, not_6_out, not_7_out);
  and and_63 (and_63_out, B8, not_2_out, B6, not_5_out, B3);
  and and_64 (and_64_out, B8, B6, not_4_out, not_5_out, B3, B2);
  and and_65 (and_65_out, B8, not_2_out, B6, B5, B4, not_6_out);
  and and_66 (and_66_out, B8, not_2_out, B6, B5, B4, not_7_out);
  and and_67 (and_67_out, B8, B7, not_3_out, B5, not_6_out, B2);
  and and_68 (and_68_out, B8, B7, B6, not_4_out, B4);
  and and_69 (and_69_out, not_1_out, not_2_out, not_4_out, not_5_out, B3, B1);
  and and_70 (and_70_out, not_1_out, not_2_out, not_4_out, not_5_out, B3, B2);
  and and_71 (and_71_out, not_1_out, not_2_out, not_4_out, B3, B2, B1);
  and and_72 (and_72_out, not_2_out, not_4_out, not_5_out, B3, B2, B1);
  and and_73 (and_73_out, not_2_out, not_3_out, not_4_out, B4, not_6_out, not_7_out);
  and and_74 (and_74_out, not_1_out, not_2_out, not_3_out, B5, not_5_out, not_6_out);
  and and_75 (and_75_out, not_1_out, not_2_out, not_3_out, B5, not_6_out, B1);
  and and_76 (and_76_out, not_2_out, not_3_out, B5, not_5_out, not_6_out, B1);
  and and_77 (and_77_out, not_1_out, not_2_out, not_3_out, B5, not_6_out, B2);
  and and_78 (and_78_out, not_2_out, not_3_out, B5, not_5_out, not_6_out, B2);
  and and_79 (and_79_out, not_2_out, not_3_out, B5, not_6_out, B2, B1);
  and and_80 (and_80_out, not_2_out, not_3_out, B5, B4, B3, not_7_out);
  and and_81 (and_81_out, not_1_out, not_2_out, B6, not_4_out, not_5_out, B2, B1);
  and and_82 (and_82_out, not_1_out, not_2_out, B6, not_4_out, not_5_out, B3);
  and and_83 (and_83_out, not_1_out, not_2_out, B6, not_4_out, B3, B1);
  and and_84 (and_84_out, not_2_out, B6, not_4_out, not_5_out, B3, B1);
  and and_85 (and_85_out, not_1_out, not_2_out, B6, not_4_out, B3, B2);
  and and_86 (and_86_out, not_2_out, B6, not_4_out, not_5_out, B3, B2);
  and and_87 (and_87_out, not_1_out, not_2_out, B6, not_5_out, B3, B2, B1);
  and and_88 (and_88_out, not_2_out, B6, not_4_out, B3, B2, B1);
  and and_89 (and_89_out, not_1_out, not_2_out, B6, B5, not_6_out, not_7_out);
  and and_90 (and_90_out, not_2_out, B6, B5, not_5_out, not_6_out, not_7_out);
  and and_91 (and_91_out, not_2_out, B6, B5, not_6_out, not_7_out, B1);
  and and_92 (and_92_out, not_2_out, B6, B5, B4, not_6_out, B2);
  and and_93 (and_93_out, not_1_out, B7, not_4_out, not_5_out, not_6_out, B1);
  and and_94 (and_94_out, not_1_out, B7, not_4_out, not_5_out, not_6_out, B2);
  and and_95 (and_95_out, not_1_out, B7, not_4_out, not_6_out, B2, B1);
  and and_96 (and_96_out, B7, not_4_out, not_5_out, not_6_out, B2, B1);
  and and_97 (and_97_out, B7, not_3_out, not_4_out, not_5_out, B3, not_7_out);
  and and_98 (and_98_out, B7, not_3_out, not_4_out, B3, not_7_out, B1);
  and and_99 (and_99_out, not_1_out, B7, not_3_out, not_4_out, B4, B3);
  and and_100 (and_100_out, not_1_out, B7, not_4_out, B4, B3, not_7_out);
  and and_101 (and_101_out, not_1_out, B7, B5, not_5_out, B3, B1);
  and and_102 (and_102_out, not_1_out, B7, B5, not_5_out, B3, B2);
  and and_103 (and_103_out, not_1_out, B7, B5, B3, B2, B1);
  and and_104 (and_104_out, B7, B5, not_5_out, B3, B2, B1);
  and and_105 (and_105_out, B7, not_3_out, B5, B4, not_6_out, not_7_out);
  and and_106 (and_106_out, not_1_out, B7, B6, not_4_out, not_5_out, not_6_out);
  and and_107 (and_107_out, not_1_out, B7, B6, not_4_out, not_6_out, B1);
  and and_108 (and_108_out, B7, B6, not_4_out, not_5_out, not_6_out, B1);
  and and_109 (and_109_out, not_1_out, B7, B6, not_4_out, not_6_out, B2);
  and and_110 (and_110_out, B7, B6, not_4_out, not_5_out, not_6_out, B2);
  and and_111 (and_111_out, not_1_out, B7, B6, not_5_out, not_6_out, B2, B1);
  and and_112 (and_112_out, B7, B6, not_4_out, not_6_out, B2, B1);
  and and_113 (and_113_out, not_1_out, B7, B6, B5, not_5_out, B3);
  and and_114 (and_114_out, not_1_out, B7, B6, B5, B3, B1);
  and and_115 (and_115_out, B7, B6, B5, not_5_out, B3, B1);
  and and_116 (and_116_out, not_1_out, B7, B6, B5, B3, B2);
  and and_117 (and_117_out, B7, B6, B5, not_5_out, B3, B2);
  and and_118 (and_118_out, B7, B6, B5, B3, B2, B1);
  and and_119 (and_119_out, B8, not_2_out, not_3_out, not_4_out, not_6_out, not_7_out);
  and and_120 (and_120_out, B8, not_2_out, not_3_out, not_4_out, B4, not_6_out);
  and and_121 (and_121_out, B8, not_2_out, not_4_out, B4, not_6_out, not_7_out);
  and and_122 (and_122_out, B8, not_2_out, not_3_out, B5, B3, not_7_out);
  and and_123 (and_123_out, B8, not_2_out, not_3_out, B5, B4, B3);
  and and_124 (and_124_out, B8, not_2_out, B5, B4, B3, not_7_out);
  and and_125 (and_125_out, B8, not_2_out, B6, B5, not_6_out, B2);
  and and_126 (and_126_out, B8, B7, not_3_out, not_4_out, not_5_out, B3);
  and and_127 (and_127_out, B8, B7, not_4_out, not_5_out, B3, not_7_out);
  and and_128 (and_128_out, B8, B7, not_4_out, B4, B3, B2);
  and and_129 (and_129_out, B8, B7, not_3_out, B5, not_6_out, not_7_out);
  and and_130 (and_130_out, B8, B7, not_3_out, B5, B4, not_6_out);
  and and_131 (and_131_out, B8, B7, B5, B4, not_6_out, not_7_out);
  and and_132 (and_132_out, B8, B7, B6, not_4_out, B4, B3);
  and and_133 (and_133_out, not_1_out, not_2_out, not_3_out, not_4_out, not_5_out, B3, not_7_out, not_8_out);
  and and_134 (and_134_out, not_1_out, not_2_out, not_3_out, not_4_out, B4, not_6_out, not_7_out, B1);
  and and_135 (and_135_out, not_1_out, not_2_out, not_3_out, not_4_out, B4, B3, B2, not_8_out);
  and and_136 (and_136_out, not_1_out, not_2_out, not_3_out, B5, not_5_out, not_6_out, B2, B1);
  and and_137 (and_137_out, not_1_out, not_2_out, not_3_out, B5, B4, not_6_out, not_7_out, not_8_out);
  and and_138 (and_138_out, not_1_out, not_2_out, not_3_out, B5, B4, B3, not_7_out, B1);
  and and_139 (and_139_out, not_1_out, not_2_out, B6, not_4_out, not_5_out, not_6_out, B2, not_8_out);
  and and_140 (and_140_out, not_1_out, not_2_out, B6, not_4_out, not_5_out, B3, B2, B1);
  and and_141 (and_141_out, not_1_out, not_2_out, B6, not_4_out, B4, B3, not_7_out, not_8_out);
  and and_142 (and_142_out, not_1_out, not_2_out, B6, B5, not_5_out, not_6_out, not_7_out, B1);
  and and_143 (and_143_out, not_1_out, not_2_out, B6, B5, not_5_out, B3, B2, not_8_out);
  and and_144 (and_144_out, not_1_out, not_2_out, B6, B5, B4, not_6_out, B2, B1);
  and and_145 (and_145_out, not_1_out, B7, not_3_out, not_4_out, not_5_out, not_6_out, not_7_out, not_8_out);
  and and_146 (and_146_out, not_1_out, B7, not_3_out, not_4_out, not_5_out, B3, not_7_out, B1);
  and and_147 (and_147_out, not_1_out, B7, not_3_out, not_4_out, B4, not_6_out, B2, not_8_out);
  and and_148 (and_148_out, not_1_out, B7, not_3_out, not_4_out, B4, B3, B2, B1);
  and and_149 (and_149_out, not_1_out, B7, not_3_out, B5, not_5_out, B3, not_7_out, not_8_out);
  and and_150 (and_150_out, not_1_out, B7, not_3_out, B5, B4, not_6_out, not_7_out, B1);
  and and_151 (and_151_out, not_1_out, B7, not_3_out, B5, B4, B3, B2, not_8_out);
  and and_152 (and_152_out, not_1_out, B7, B6, not_4_out, not_5_out, not_6_out, B2, B1);
  and and_153 (and_153_out, not_1_out, B7, B6, not_4_out, B4, not_6_out, not_7_out, not_8_out);
  and and_154 (and_154_out, not_1_out, B7, B6, not_4_out, B4, B3, not_7_out, B1);
  and and_155 (and_155_out, not_1_out, B7, B6, B5, not_5_out, not_6_out, B2, not_8_out);
  and and_156 (and_156_out, not_1_out, B7, B6, B5, not_5_out, B3, B2, B1);
  and and_157 (and_157_out, not_1_out, B7, B6, B5, B4, B3, not_7_out, not_8_out);
  and and_158 (and_158_out, B8, not_2_out, not_3_out, not_4_out, not_5_out, not_6_out, not_7_out, B1);
  and and_159 (and_159_out, B8, not_2_out, not_3_out, not_4_out, not_5_out, B3, B2, not_8_out);
  and and_160 (and_160_out, B8, not_2_out, not_3_out, not_4_out, B4, not_6_out, B2, B1);
  and and_161 (and_161_out, B8, not_2_out, not_3_out, B5, not_5_out, not_6_out, not_7_out, not_8_out);
  and and_162 (and_162_out, B8, not_2_out, not_3_out, B5, not_5_out, B3, not_7_out, B1);
  and and_163 (and_163_out, B8, not_2_out, not_3_out, B5, B4, not_6_out, B2, not_8_out);
  and and_164 (and_164_out, B8, not_2_out, not_3_out, B5, B4, B3, B2, B1);
  and and_165 (and_165_out, B8, not_2_out, B6, not_4_out, not_5_out, B3, not_7_out, not_8_out);
  and and_166 (and_166_out, B8, not_2_out, B6, not_4_out, B4, not_6_out, not_7_out, B1);
  and and_167 (and_167_out, B8, not_2_out, B6, not_4_out, B4, B3, B2, not_8_out);
  and and_168 (and_168_out, B8, not_2_out, B6, B5, not_5_out, not_6_out, B2, B1);
  and and_169 (and_169_out, B8, not_2_out, B6, B5, B4, not_6_out, not_7_out, not_8_out);
  and and_170 (and_170_out, B8, not_2_out, B6, B5, B4, B3, not_7_out, B1);
  and and_171 (and_171_out, B8, B7, not_3_out, not_4_out, not_5_out, not_6_out, B2, not_8_out);
  and and_172 (and_172_out, B8, B7, not_3_out, not_4_out, not_5_out, B3, B2, B1);
  and and_173 (and_173_out, B8, B7, not_3_out, not_4_out, B4, B3, not_7_out, not_8_out);
  and and_174 (and_174_out, B8, B7, not_3_out, B5, not_5_out, not_6_out, not_7_out, B1);
  and and_175 (and_175_out, B8, B7, not_3_out, B5, not_5_out, B3, B2, not_8_out);
  and and_176 (and_176_out, B8, B7, not_3_out, B5, B4, not_6_out, B2, B1);
  and and_177 (and_177_out, B8, B7, B6, not_4_out, not_5_out, not_6_out, not_7_out, not_8_out);
  and and_178 (and_178_out, B8, B7, B6, not_4_out, not_5_out, B3, not_7_out, B1);
  and and_179 (and_179_out, B8, B7, B6, not_4_out, B4, not_6_out, B2, not_8_out);
  and and_180 (and_180_out, B8, B7, B6, not_4_out, B4, B3, B2, B1);
  and and_181 (and_181_out, B8, B7, B6, B5, not_5_out, B3, not_7_out, not_8_out);
  and and_182 (and_182_out, B8, B7, B6, B5, B4, not_6_out, not_7_out, B1);
  and and_183 (and_183_out, B8, B7, B6, B5, B4, B3, B2, not_8_out);
  and and_184 (and_184_out, not_1_out, not_2_out, not_3_out, not_4_out, not_5_out, not_6_out, B2);
  and and_185 (and_185_out, not_1_out, not_2_out, not_3_out, not_4_out, not_5_out, B2, B1);
  and and_186 (and_186_out, not_1_out, not_3_out, not_4_out, not_5_out, not_6_out, B2, B1);
  and and_187 (and_187_out, not_1_out, not_2_out, not_3_out, not_4_out, B4, not_7_out, not_8_out);
  and and_188 (and_188_out, not_1_out, not_2_out, not_3_out, not_4_out, B4, B3, not_7_out);
  and and_189 (and_189_out, not_1_out, not_2_out, not_3_out, B4, B3, not_7_out, not_8_out);
  and and_190 (and_190_out, not_1_out, not_2_out, not_3_out, B5, not_5_out, not_6_out, not_7_out, B1);
  and and_191 (and_191_out, not_1_out, not_2_out, not_3_out, B5, not_5_out, B2, not_8_out);
  and and_192 (and_192_out, not_1_out, not_3_out, B5, not_5_out, not_6_out, B2, not_8_out);
  and and_193 (and_193_out, not_1_out, not_3_out, B5, not_5_out, B3, B2, B1);
  and and_194 (and_194_out, not_1_out, not_2_out, not_3_out, B5, B4, not_6_out, B2, B1);
  and and_195 (and_195_out, not_1_out, not_2_out, B6, not_4_out, not_5_out, not_6_out, not_7_out);
  and and_196 (and_196_out, not_1_out, not_2_out, B6, not_4_out, not_5_out, not_7_out, B1);
  and and_197 (and_197_out, not_1_out, B6, not_4_out, not_5_out, not_6_out, not_7_out, B1);
  and and_198 (and_198_out, not_1_out, B6, not_4_out, not_5_out, B3, B2, not_8_out);
  and and_199 (and_199_out, not_1_out, not_2_out, B6, not_4_out, B4, not_6_out, B2);
  and and_200 (and_200_out, not_1_out, not_2_out, B6, not_4_out, B4, B2, B1);
  and and_201 (and_201_out, not_1_out, B6, not_4_out, B4, not_6_out, B2, B1);
  and and_202 (and_202_out, not_1_out, not_2_out, B6, B5, not_5_out, not_7_out, not_8_out);
  and and_203 (and_203_out, not_1_out, B6, B5, not_5_out, not_6_out, not_7_out, not_8_out);
  and and_204 (and_204_out, not_1_out, B6, B5, not_5_out, B3, not_7_out, B1);
  and and_205 (and_205_out, not_1_out, not_2_out, B6, B5, B4, not_6_out, not_7_out, B1);
  and and_206 (and_206_out, not_1_out, not_2_out, B6, B5, B4, B2, not_8_out);
  and and_207 (and_207_out, not_1_out, B6, B5, B4, not_6_out, B2, not_8_out);
  and and_208 (and_208_out, not_1_out, B6, B5, B4, B3, B2, B1);
  and and_209 (and_209_out, not_1_out, B7, not_3_out, not_4_out, not_5_out, B3, not_7_out, not_8_out);
  and and_210 (and_210_out, not_1_out, B7, not_3_out, not_4_out, B4, not_6_out, not_7_out);
  and and_211 (and_211_out, not_1_out, B7, not_3_out, B4, not_6_out, not_7_out, not_8_out);
  and and_212 (and_212_out, not_1_out, B7, not_3_out, B4, B3, not_7_out, B1);
  and and_213 (and_213_out, not_1_out, B7, not_3_out, not_4_out, B4, B3, B2, not_8_out);
  and and_214 (and_214_out, not_1_out, B7, not_3_out, B5, not_5_out, B2, B1);
  and and_215 (and_215_out, not_1_out, B7, not_3_out, B5, B4, B3, not_7_out);
  and and_216 (and_216_out, not_1_out, B7, B6, not_4_out, not_5_out, B2, not_8_out);
  and and_217 (and_217_out, not_1_out, B7, B6, not_4_out, not_5_out, B3, B2);
  and and_218 (and_218_out, not_1_out, B7, B6, not_5_out, B3, B2, not_8_out);
  and and_219 (and_219_out, not_1_out, B7, B6, not_4_out, B4, B3, not_7_out, not_8_out);
  and and_220 (and_220_out, not_1_out, B7, B6, B5, not_5_out, not_7_out, B1);
  and and_221 (and_221_out, not_1_out, B7, B6, B5, B4, B2, B1);
  and and_222 (and_222_out, B8, not_2_out, not_3_out, not_4_out, not_5_out, not_7_out, not_8_out);
  and and_223 (and_223_out, B8, not_2_out, not_3_out, not_4_out, not_5_out, B3, not_7_out);
  and and_224 (and_224_out, B8, not_2_out, not_3_out, not_5_out, B3, not_7_out, not_8_out);
  and and_225 (and_225_out, B8, not_2_out, not_3_out, B4, not_6_out, not_7_out, B1);
  and and_226 (and_226_out, B8, not_2_out, not_3_out, not_4_out, B4, B2, not_8_out);
  and and_227 (and_227_out, B8, not_2_out, not_3_out, not_4_out, B4, B3, B2);
  and and_228 (and_228_out, B8, not_2_out, not_3_out, B4, B3, B2, not_8_out);
  and and_229 (and_229_out, B8, not_2_out, not_3_out, B5, not_5_out, not_6_out, B2, B1);
  and and_230 (and_230_out, B8, not_2_out, not_3_out, B5, B4, not_6_out, not_7_out);
  and and_231 (and_231_out, B8, not_2_out, not_3_out, B5, B4, not_7_out, B1);
  and and_232 (and_232_out, B8, not_3_out, B5, B4, not_6_out, not_7_out, B1);
  and and_233 (and_233_out, B8, not_2_out, B6, not_4_out, not_5_out, not_6_out, B2);
  and and_234 (and_234_out, B8, not_2_out, B6, not_4_out, not_5_out, B2, B1);
  and and_235 (and_235_out, B8, B6, not_4_out, not_5_out, not_6_out, B2, B1);
  and and_236 (and_236_out, B8, not_2_out, B6, not_4_out, B4, not_7_out, not_8_out);
  and and_237 (and_237_out, B8, not_2_out, B6, not_4_out, B4, B3, not_7_out);
  and and_238 (and_238_out, B8, not_2_out, B6, B4, B3, not_7_out, not_8_out);
  and and_239 (and_239_out, B8, not_2_out, B6, B5, not_5_out, not_6_out, not_7_out, B1);
  and and_240 (and_240_out, B8, not_2_out, B6, B5, not_5_out, B2, not_8_out);
  and and_241 (and_241_out, B8, B6, B5, not_5_out, not_6_out, B2, not_8_out);
  and and_242 (and_242_out, B8, B6, B5, not_5_out, B3, B2, B1);
  and and_243 (and_243_out, B8, not_2_out, B6, B5, B4, not_6_out, B2, B1);
  and and_244 (and_244_out, B8, B7, not_3_out, not_4_out, not_5_out, not_6_out, not_7_out);
  and and_245 (and_245_out, B8, B7, not_3_out, not_5_out, not_6_out, not_7_out, not_8_out);
  and and_246 (and_246_out, B8, B7, not_3_out, not_5_out, B3, not_7_out, B1);
  and and_247 (and_247_out, B8, B7, not_3_out, not_4_out, not_5_out, B3, B2, not_8_out);
  and and_248 (and_248_out, B8, B7, not_3_out, not_4_out, B4, not_6_out, B2);
  and and_249 (and_249_out, B8, B7, not_3_out, B4, not_6_out, B2, not_8_out);
  and and_250 (and_250_out, B8, B7, not_3_out, B4, B3, B2, B1);
  and and_251 (and_251_out, B8, B7, not_3_out, B5, not_5_out, B3, not_7_out);
  and and_252 (and_252_out, B8, B7, not_3_out, B5, B4, B3, B2);
  and and_253 (and_253_out, B8, B7, B6, not_4_out, not_5_out, B3, not_7_out, not_8_out);
  and and_254 (and_254_out, B8, B7, B6, not_4_out, B4, not_6_out, not_7_out);
  and and_255 (and_255_out, B8, B7, B6, B4, not_6_out, not_7_out, not_8_out);
  and and_256 (and_256_out, B8, B7, B6, B4, B3, not_7_out, B1);
  and and_257 (and_257_out, B8, B7, B6, not_4_out, B4, B3, B2, not_8_out);
  and and_258 (and_258_out, B8, B7, B6, B5, not_5_out, B2, B1);
  and and_259 (and_259_out, B8, B7, B6, B5, B4, B3, not_7_out);
  and and_260 (and_260_out, not_1_out, not_2_out, not_3_out, not_4_out, not_5_out, not_6_out, B1);
  and and_261 (and_261_out, not_1_out, not_2_out, not_3_out, not_4_out, not_6_out, B2, B1);
  and and_262 (and_262_out, not_2_out, not_3_out, not_4_out, not_5_out, not_6_out, B2, B1);
  and and_263 (and_263_out, not_1_out, not_2_out, not_4_out, not_5_out, B3, B2, not_8_out);
  and and_264 (and_264_out, not_2_out, not_3_out, not_4_out, B4, not_6_out, not_7_out, not_8_out);
  and and_265 (and_265_out, not_2_out, not_3_out, not_4_out, B4, B3, not_7_out, B1);
  and and_266 (and_266_out, not_1_out, not_2_out, not_3_out, B5, not_5_out, not_6_out, not_8_out);
  and and_267 (and_267_out, not_1_out, not_2_out, not_3_out, B5, not_6_out, B2, not_8_out);
  and and_268 (and_268_out, not_2_out, not_3_out, B5, not_5_out, not_6_out, B2, not_8_out);
  and and_269 (and_269_out, not_1_out, not_2_out, not_3_out, B5, not_5_out, B3, B1);
  and and_270 (and_270_out, not_1_out, not_2_out, not_3_out, B5, B3, B2, B1);
  and and_271 (and_271_out, not_2_out, not_3_out, B5, not_5_out, B3, B2, B1);
  and and_272 (and_272_out, not_2_out, not_3_out, B5, B4, B3, not_7_out, not_8_out);
  and and_273 (and_273_out, not_1_out, not_2_out, B6, not_4_out, not_6_out, not_7_out, B1);
  and and_274 (and_274_out, not_2_out, B6, not_4_out, not_5_out, not_6_out, not_7_out, B1);
  and and_275 (and_275_out, not_1_out, not_2_out, B6, not_4_out, not_5_out, B3, not_8_out);
  and and_276 (and_276_out, not_1_out, not_2_out, B6, not_4_out, B3, B2, not_8_out);
  and and_277 (and_277_out, not_2_out, B6, not_4_out, not_5_out, B3, B2, not_8_out);
  and and_278 (and_278_out, not_2_out, B6, not_4_out, B4, not_6_out, B2, B1);
  and and_279 (and_279_out, not_1_out, not_2_out, B6, B5, not_6_out, not_7_out, not_8_out);
  and and_280 (and_280_out, not_2_out, B6, B5, not_5_out, not_6_out, not_7_out, not_8_out);
  and and_281 (and_281_out, not_1_out, not_2_out, B6, B5, not_5_out, not_6_out, B2, B1);
  and and_282 (and_282_out, not_1_out, not_2_out, B6, B5, B3, not_7_out, B1);
  and and_283 (and_283_out, not_2_out, B6, B5, not_5_out, B3, not_7_out, B1);
  and and_284 (and_284_out, not_2_out, B6, B5, B4, not_6_out, B2, not_8_out);
  and and_285 (and_285_out, not_2_out, B6, B5, B4, B3, B2, B1);
  and and_286 (and_286_out, not_1_out, B7, not_4_out, not_5_out, not_6_out, B2, not_8_out);
  and and_287 (and_287_out, B7, not_3_out, not_4_out, not_5_out, B3, not_7_out, not_8_out);
  and and_288 (and_288_out, not_1_out, B7, not_4_out, not_5_out, B3, B2, B1);
  and and_289 (and_289_out, B7, not_3_out, not_4_out, B4, not_6_out, not_7_out, B1);
  and and_290 (and_290_out, not_1_out, B7, not_3_out, not_4_out, B4, B3, not_8_out);
  and and_291 (and_291_out, not_1_out, B7, not_4_out, B4, B3, not_7_out, not_8_out);
  and and_292 (and_292_out, not_1_out, B7, not_3_out, B5, not_5_out, not_6_out, B1);
  and and_293 (and_293_out, not_1_out, B7, not_3_out, B5, not_6_out, B2, B1);
  and and_294 (and_294_out, B7, not_3_out, B5, not_5_out, not_6_out, B2, B1);
  and and_295 (and_295_out, not_1_out, B7, B5, not_5_out, B3, B2, not_8_out);
  and and_296 (and_296_out, B7, not_3_out, B5, B4, not_6_out, not_7_out, not_8_out);
  and and_297 (and_297_out, B7, not_3_out, B5, B4, B3, not_7_out, B1);
  and and_298 (and_298_out, not_1_out, B7, B6, not_4_out, not_5_out, not_6_out, not_8_out);
  and and_299 (and_299_out, not_1_out, B7, B6, not_4_out, not_6_out, B2, not_8_out);
  and and_300 (and_300_out, B7, B6, not_4_out, not_5_out, not_6_out, B2, not_8_out);
  and and_301 (and_301_out, not_1_out, B7, B6, not_4_out, not_5_out, B3, B1);
  and and_302 (and_302_out, not_1_out, B7, B6, not_4_out, B3, B2, B1);
  and and_303 (and_303_out, B7, B6, not_4_out, not_5_out, B3, B2, B1);
  and and_304 (and_304_out, not_1_out, B7, B6, B5, not_6_out, not_7_out, B1);
  and and_305 (and_305_out, B7, B6, B5, not_5_out, not_6_out, not_7_out, B1);
  and and_306 (and_306_out, not_1_out, B7, B6, B5, not_5_out, B3, not_8_out);
  and and_307 (and_307_out, not_1_out, B7, B6, B5, B3, B2, not_8_out);
  and and_308 (and_308_out, B7, B6, B5, not_5_out, B3, B2, not_8_out);
  and and_309 (and_309_out, B7, B6, B5, B4, not_6_out, B2, B1);
  and and_310 (and_310_out, B8, not_2_out, not_3_out, not_4_out, not_6_out, not_7_out, not_8_out);
  and and_311 (and_311_out, B8, not_2_out, not_3_out, not_4_out, B3, not_7_out, B1);
  and and_312 (and_312_out, B8, not_2_out, not_3_out, not_4_out, B4, not_6_out, not_8_out);
  and and_313 (and_313_out, B8, not_2_out, not_4_out, B4, not_6_out, not_7_out, not_8_out);
  and and_314 (and_314_out, B8, not_2_out, not_3_out, not_4_out, B4, B3, B1);
  and and_315 (and_315_out, B8, not_2_out, not_4_out, B4, B3, not_7_out, B1);
  and and_316 (and_316_out, B8, not_2_out, not_3_out, B5, B3, not_7_out, not_8_out);
  and and_317 (and_317_out, B8, not_2_out, not_3_out, B5, B4, not_6_out, not_7_out, B1);
  and and_318 (and_318_out, B8, not_2_out, not_3_out, B5, B4, B3, not_8_out);
  and and_319 (and_319_out, B8, not_2_out, B5, B4, B3, not_7_out, not_8_out);
  and and_320 (and_320_out, B8, not_2_out, B6, not_4_out, not_6_out, B2, B1);
  and and_321 (and_321_out, B8, not_2_out, B6, B5, not_6_out, B2, not_8_out);
  and and_322 (and_322_out, B8, not_2_out, B6, B5, B3, B2, B1);
  and and_323 (and_323_out, B8, B7, not_3_out, not_4_out, not_6_out, not_7_out, B1);
  and and_324 (and_324_out, B8, B7, not_3_out, not_4_out, not_5_out, B3, not_8_out);
  and and_325 (and_325_out, B8, B7, not_4_out, not_5_out, B3, not_7_out, not_8_out);
  and and_326 (and_326_out, B8, B7, not_3_out, not_4_out, B4, not_6_out, B1);
  and and_327 (and_327_out, B8, B7, not_4_out, B4, not_6_out, not_7_out, B1);
  and and_328 (and_328_out, B8, B7, not_4_out, B4, B3, B2, not_8_out);
  and and_329 (and_329_out, B8, B7, not_3_out, B5, not_6_out, not_7_out, not_8_out);
  and and_330 (and_330_out, B8, B7, not_3_out, B5, B3, not_7_out, B1);
  and and_331 (and_331_out, B8, B7, not_3_out, B5, B4, not_6_out, not_8_out);
  and and_332 (and_332_out, B8, B7, B5, B4, not_6_out, not_7_out, not_8_out);
  and and_333 (and_333_out, B8, B7, not_3_out, B5, B4, B3, B1);
  and and_334 (and_334_out, B8, B7, B5, B4, B3, not_7_out, B1);
  and and_335 (and_335_out, B8, B7, B6, not_4_out, B4, B3, not_8_out);
  and and_336 (and_336_out, B8, B7, B6, B5, not_6_out, B2, B1);
  or or_2 (out_10[9], and_4_out, and_5_out, and_6_out, and_7_out, and_8_out);
  or or_3 (out_10[8], and_9_out, and_10_out, and_11_out, and_12_out, and_13_out, and_14_out, and_15_out, and_16_out, and_17_out, and_18_out, and_19_out);
  or or_4 (out_10[7], and_20_out, and_21_out, and_22_out, and_23_out, and_24_out, and_25_out, and_26_out, and_27_out, and_28_out, and_29_out, and_30_out, and_31_out);
  or or_5 (out_10[6], and_32_out, and_33_out, and_34_out, and_35_out, and_36_out, and_37_out, and_38_out, and_39_out, and_40_out, and_41_out, and_42_out, and_43_out, and_44_out, and_45_out, and_46_out, and_47_out);
  or or_6 (out_10[5], and_48_out, and_49_out, and_50_out, and_51_out, and_52_out, and_53_out, and_54_out, and_55_out, and_56_out, and_57_out, and_58_out, and_59_out, and_60_out, and_61_out, and_62_out, and_63_out, and_64_out, and_65_out, and_66_out, and_67_out, and_68_out);
  or or_7 (out_10[3], and_133_out, and_134_out, and_135_out, and_136_out, and_137_out, and_138_out, and_139_out, and_140_out, and_141_out, and_142_out, and_143_out, and_144_out, and_145_out, and_146_out, and_147_out, and_148_out, and_149_out, and_150_out, and_151_out, and_152_out, and_153_out, and_154_out, and_155_out, and_156_out, and_157_out, and_158_out, and_159_out, and_160_out, and_161_out, and_162_out, and_163_out, and_164_out, and_165_out, and_166_out, and_167_out, and_168_out, and_169_out, and_170_out, and_171_out, and_172_out, and_173_out, and_174_out, and_175_out, and_176_out, and_177_out, and_178_out, and_179_out, and_180_out, and_181_out, and_182_out, and_183_out);
  or or_8 (or_8_out, and_184_out, and_185_out, and_186_out, and_187_out, and_188_out, and_189_out, and_190_out, and_191_out, and_192_out, and_193_out, and_194_out, and_195_out, and_196_out, and_197_out, and_198_out, and_199_out, and_200_out, and_201_out, and_202_out, and_203_out, and_204_out, and_205_out, and_206_out, and_207_out, and_208_out, and_209_out, and_210_out, and_211_out, and_212_out, and_213_out, and_214_out, and_215_out, and_216_out, and_217_out, and_218_out, and_219_out, and_220_out, and_221_out);
  or or_9 (or_9_out, and_222_out, and_223_out, and_224_out, and_225_out, and_226_out, and_227_out, and_228_out, and_229_out, and_230_out, and_231_out, and_232_out, and_233_out, and_234_out, and_235_out, and_236_out, and_237_out, and_238_out, and_239_out, and_240_out, and_241_out, and_242_out, and_243_out, and_244_out, and_245_out, and_246_out, and_247_out, and_248_out, and_249_out, and_250_out, and_251_out, and_252_out, and_253_out, and_254_out, and_255_out, and_256_out, and_257_out, and_258_out, and_259_out);
  or or_10 (or_10_out, and_260_out, and_261_out, and_262_out, and_263_out, and_264_out, and_265_out, and_266_out, and_267_out, and_268_out, and_269_out, and_270_out, and_271_out, and_272_out, and_273_out, and_274_out, and_275_out, and_276_out, and_277_out, and_278_out, and_279_out, and_280_out, and_281_out, and_282_out, and_283_out, and_284_out, and_285_out, and_286_out, and_287_out, and_288_out, and_289_out, and_290_out, and_291_out, and_292_out, and_293_out, and_294_out, and_295_out, and_296_out, and_297_out, and_298_out);
  or or_11 (or_11_out, and_299_out, and_300_out, and_301_out, and_302_out, and_303_out, and_304_out, and_305_out, and_306_out, and_307_out, and_308_out, and_309_out, and_310_out, and_311_out, and_312_out, and_313_out, and_314_out, and_315_out, and_316_out, and_317_out, and_318_out, and_319_out, and_320_out, and_321_out, and_322_out, and_323_out, and_324_out, and_325_out, and_326_out, and_327_out, and_328_out, and_329_out, and_330_out, and_331_out, and_332_out, and_333_out, and_334_out, and_335_out, and_336_out);
  or or_12 (out_10[4], and_69_out, and_70_out, and_71_out, and_72_out, and_73_out, and_74_out, and_75_out, and_76_out, and_77_out, and_78_out, and_79_out, and_80_out, and_81_out, and_82_out, and_83_out, and_84_out, and_85_out, and_86_out, and_87_out, and_88_out, and_89_out, and_90_out, and_91_out, and_92_out, and_93_out, and_94_out, and_95_out, and_96_out, and_97_out, and_98_out, and_99_out, and_100_out, and_101_out, and_102_out, and_103_out, and_104_out, and_105_out, and_106_out, and_107_out, and_108_out, and_109_out, and_110_out, and_111_out, and_112_out, and_113_out, and_114_out, and_115_out, and_116_out, and_117_out, and_118_out, and_119_out, and_120_out, and_121_out, and_122_out, and_123_out, and_124_out, and_125_out, and_126_out, and_127_out, and_128_out, and_129_out, and_130_out, and_131_out, and_132_out);
  or or_13 (out_10[2], or_8_out, or_9_out);
  or or_14 (out_10[1], or_10_out, or_11_out);

  assign {out_10[11], out_10[0]} = {1'b0, B0};
endmodule

module pass_bin (
  input  [8:0] in_1,
  input  Sign_1,
  output [3:0] lsb,
  output [3:0] mid,
  output [3:0] msb
);

  wire [8:0] adder_1_out, multiplexer_1_out, not_1_out;

  assign not_1_out = ~in_1;  // NOT_Gate not_1, 9 bits wide
  Adder #(.width(9)) adder_1 (.a(not_1_out), .b({9{1'b0}}), .out(adder_1_out), .cin(1'b1));  // open: cout
  Multiplexer #(.width(9)) multiplexer_1 (.in0(in_1), .in1(adder_1_out), .out(multiplexer_1_out), .sel(Sign_1));
  bin_bcd_9bits bin_bcd_9bits_1 (
    .out_10({msb, mid, lsb}), .B8(multiplexer_1_out[8]), .B7(multiplexer_1_out[7]),
    .B6(multiplexer_1_out[6]), .B5(multiplexer_1_out[5]), .B4(multiplexer_1_out[4]),
    .B3(multiplexer_1_out[3]), .B2(multiplexer_1_out[2]), .B1(multiplexer_1_out[1]), .B0(multiplexer_1_out[0]));
endmodule

module seven_seg (
  input  [3:0] in_1,
  output a,
  output b,
  output c,
  output d,
  output e,
  output f,
  output g
);

  wire and_1_out, and_2_out, and_3_out, and_4_out, and_5_out, and_6_out, and_7_out, and_8_out, and_9_out,
       and_10_out, and_11_out, and_12_out, not_1_out, not_2_out, not_3_out, not_4_out, xnor_1_out, xnor_2_out;

  not not_1 (not_1_out, in_1[3]);
  not not_2 (not_2_out, in_1[2]);
  not not_3 (not_3_out, in_1[1]);
  not not_4 (not_4_out, in_1[0]);
  xnor xnor_1 (xnor_1_out, in_1[0], in_1[2]);
  xnor xnor_2 (xnor_2_out, in_1[0], in_1[1]);
  and and_1 (and_1_out, not_4_out, in_1[1]);
  and and_2 (and_2_out, not_2_out, in_1[1]);
  and and_3 (and_3_out, in_1[0], not_3_out, in_1[2]);
  and and_4 (and_4_out, not_4_out, not_2_out);
  and and_5 (and_5_out, not_4_out, in_1[1]);
  and and_6 (and_6_out, not_4_out, not_2_out);
  and and_7 (and_7_out, not_3_out, in_1[2]);
  and and_8 (and_8_out, not_4_out, not_3_out);
  and and_9 (and_9_out, not_4_out, in_1[2]);
  and and_10 (and_10_out, not_3_out, in_1[2]);
  and and_11 (and_11_out, not_4_out, in_1[1]);
  and and_12 (and_12_out, not_2_out, in_1[1]);
  or or_1 (a, in_1[1], in_1[3], xnor_1_out);
  or or_2 (b, not_2_out, xnor_2_out);
  or or_3 (c, in_1[2], not_3_out, in_1[0]);
  or or_4 (d, and_1_out, and_2_out, in_1[3], and_3_out, and_4_out);
  or or_5 (e, and_5_out, and_6_out);
  or or_6 (f, in_1[3], and_7_out, and_8_out, and_9_out);
  or or_7 (g, in_1[3], and_10_out, and_11_out, and_12_out);
endmodule
